// Logisim project MMU.circ as structural Verilog: 4 circuits, main circuit MMU
module MMU (
  input  [31:0] Address,
  input  [31:0] WriteData,
  input  Read,
  input  Write,
  input  [1:0] Mode,
  input  SignExt,
  input  [6:0] KBD_RdData,
  input  KBD_AVAIL,
  input  CLK,
  output [6:0] TTY_WrData,
  output TTY_Write,
  output TTY_Clear,
  output KBD_ReadEn,
  output KBD_Clear,
  output [29:0] DISP_WrData,
  output DISP_Write,
  output DISP_Clear,
  output INV,
  output [31:0] Out,
  output [31:0] MTX_WrData,
  output MTX_Write,
  output [4:0] MTX_WrAddr
);

  wire and_1_out, and_4_out, and_8_out, and_9_out, and_10_out, and_11_out, and_12_out, comparator_2_eq,
       comparator_3_eq, comparator_4_eq, comparator_5_eq, comparator_7_eq, comparator_8_eq, comparator_9_eq,
       comparator_10_eq, comparator_11_eq, comparator_12_eq, controlled_buffer_1_out, DISP_SEL, DISP_WINV,
       DISP_Wr_Controller_write_2, KBD_AINV, KBD_RINV, KBD_SEL, KBD_WINV, KBD_Wr_Controller_write_2, MTX_SEL,
       MTX_WINV, multiplexer_3_out, multiplexer_5_out, or_1_out, or_2_out, or_3_out, or_4_out, or_5_out,
       or_6_out, RAM_RINV, RAM_SEL, RAM_WINV, RAM_Wr_Controller_write_2, ROM_RINV, ROM_SEL, ROM_WINV,
       TTY_SEL, TTY_WINV, TTY_Wr_Controller_write_2;
  wire [31:0] bit_extender_1_out, bit_extender_2_out, KBD_RDOut, KBD_Wr_Controller_dataout,
       multiplexer_1_out, RAM_DATA, RAM_RDOut, RAM_Wr_Controller_dataout, ROM_DATA, ROM_RDOut;
  wire [31:7] TTY_Wr_Controller_dataout;
  wire [31:30] DISP_Wr_Controller_dataout;

  Comparator #(.width(16), .mode("unsigned")) comparator_1 (
    .a(Address[31:16]), .b(16'hff), .eq(RAM_SEL));  // open: gt, lt
  Comparator #(.width(16), .mode("unsigned")) comparator_2 (
    .a(Address[31:16]), .b({16{1'b1}}), .eq(comparator_2_eq));  // open: gt, lt
  Comparator #(.width(16), .mode("unsigned")) comparator_3 (
    .a(Address[31:16]), .b({16{1'b1}}), .eq(comparator_3_eq));  // open: gt, lt
  Comparator #(.width(16), .mode("unsigned")) comparator_4 (
    .a(Address[31:16]), .b({16{1'b1}}), .eq(comparator_4_eq));  // open: gt, lt
  or or_1 (or_1_out, ROM_RINV, ROM_WINV);
  or or_2 (or_2_out, RAM_RINV, RAM_WINV);
  or or_3 (or_3_out, Address[3], TTY_WINV);
  or or_4 (or_4_out, KBD_RINV, KBD_AINV, KBD_WINV);
  or or_5 (or_5_out, Address[3], DISP_WINV);
  Comparator #(.width(16), .mode("unsigned")) comparator_5 (
    .a(Address[31:16]), .b({16{1'b1}}), .eq(comparator_5_eq));  // open: gt, lt
  Comparator #(.width(16), .mode("unsigned")) comparator_6 (
    .a(Address[31:16]), .b({16{1'b0}}), .eq(ROM_SEL));  // open: gt, lt
  and and_1 (and_1_out, Write, RAM_SEL);
  Comparator #(.width(10), .mode("unsigned")) comparator_7 (
    .a(Address[13:4]), .b({10{1'b0}}), .eq(comparator_7_eq));  // open: gt, lt
  Comparator #(.width(10), .mode("unsigned")) comparator_8 (
    .a(Address[13:4]), .b(10'hf), .eq(comparator_8_eq));  // open: gt, lt
  and and_2 (KBD_SEL, comparator_8_eq, comparator_3_eq);
  Comparator #(.width(10), .mode("unsigned")) comparator_9 (
    .a(Address[13:4]), .b(10'hff), .eq(comparator_9_eq));  // open: gt, lt
  and and_3 (DISP_SEL, comparator_9_eq, comparator_4_eq);
  assign controlled_buffer_1_out = ROM_SEL ? or_1_out : 1'bz;  // Controlled_Buffer controlled_buffer_1
  assign controlled_buffer_1_out = RAM_SEL ? or_2_out : 1'bz;  // Controlled_Buffer controlled_buffer_2
  assign controlled_buffer_1_out = TTY_SEL ? or_3_out : 1'bz;  // Controlled_Buffer controlled_buffer_3
  assign controlled_buffer_1_out = KBD_SEL ? or_4_out : 1'bz;  // Controlled_Buffer controlled_buffer_4
  assign controlled_buffer_1_out = DISP_SEL ? or_5_out : 1'bz;  // Controlled_Buffer controlled_buffer_5
  assign controlled_buffer_1_out = MTX_SEL ? MTX_WINV : 1'bz;  // Controlled_Buffer controlled_buffer_6
  and and_4 (and_4_out, ~ROM_SEL, ~RAM_SEL, ~TTY_SEL, ~KBD_SEL, ~DISP_SEL, ~MTX_SEL);  // AND_Gate
  Comparator #(.width(7), .mode("unsigned")) comparator_10 (
    .a(Address[13:7]), .b(7'b0011110), .eq(comparator_10_eq));  // open: gt, lt
  and and_5 (ROM_WINV, Write, ROM_SEL);
  Write_Align_Data RAM_Wr_Controller (
    .DataWr(WriteData), .DataPrev(RAM_DATA), .SubAddr(Address[1:0]), .Mode(Mode), .Write(and_1_out),
    .DataOut(RAM_Wr_Controller_dataout), .Invalid(RAM_WINV), .Write_2(RAM_Wr_Controller_write_2));
  and and_6 (TTY_SEL, comparator_7_eq, comparator_2_eq);
  assign controlled_buffer_1_out = and_4_out ? 1'b1 : 1'bz;  // Controlled_Buffer controlled_buffer_7
  and and_7 (MTX_SEL, comparator_10_eq, comparator_5_eq);
  ROM #(.addrWidth(12), .dataWidth(32), .Select("low")) FIRMWARE (.addr(Address[13:2]), .data(ROM_DATA), .sel(1'b0));
  RAM #(.addrWidth(12), .dataWidth(32), .bus("separate"), .Select("low")) RAM (
    .addr(Address[13:2]), .din(RAM_Wr_Controller_dataout), .data(RAM_DATA), .str(RAM_Wr_Controller_write_2),
    .sel(1'b0), .clk(CLK), .ld(1'b1), .clr(1'b0));
  and and_8 (and_8_out, Write, TTY_SEL);
  assign bit_extender_1_out = {{25{1'b0}}, KBD_RdData};  // Bit_Extender bit_extender_1
  assign bit_extender_2_out = {{31{1'b0}}, KBD_AVAIL};  // Bit_Extender bit_extender_2
  Comparator #(.width(2), .mode("unsigned")) comparator_11 (
    .a(Address[3:2]), .b(2'b10), .gt(KBD_AINV), .eq(comparator_11_eq));  // open: lt
  and and_9 (and_9_out, Write, DISP_SEL);
  Read_Align_Data ROM_Rd_Controller (
    .DataIn(ROM_DATA), .SubAddr(Address[1:0]), .Mode(Mode), .SignExt(SignExt), .DataOut(ROM_RDOut),
    .Invalid(ROM_RINV));
  and and_10 (and_10_out, Write, KBD_SEL, comparator_11_eq);
  assign Out = ROM_SEL ? ROM_RDOut : 32'bz;  // Controlled_Buffer controlled_buffer_8
  assign Out = RAM_SEL ? RAM_RDOut : 32'bz;  // Controlled_Buffer controlled_buffer_9
  assign Out = TTY_SEL ? {32{1'b0}} : 32'bz;  // Controlled_Buffer controlled_buffer_10
  assign Out = KBD_SEL ? KBD_RDOut : 32'bz;  // Controlled_Buffer controlled_buffer_11
  assign Out = DISP_SEL ? {32{1'b0}} : 32'bz;  // Controlled_Buffer controlled_buffer_12
  assign Out = and_4_out ? {32{1'b0}} : 32'bz;  // Controlled_Buffer controlled_buffer_13
  and and_11 (and_11_out, Write, MTX_SEL);
  Read_Align_Data RAM_Rd_Controller (
    .DataIn(RAM_DATA), .SubAddr(Address[1:0]), .Mode(Mode), .SignExt(SignExt), .DataOut(RAM_RDOut),
    .Invalid(RAM_RINV));
  Write_Align_Data TTY_Wr_Controller (
    .DataWr(WriteData), .DataPrev({32{1'b0}}), .SubAddr(Address[1:0]), .Mode(Mode), .Write(and_8_out),
    .DataOut({TTY_Wr_Controller_dataout, TTY_WrData}), .Invalid(TTY_WINV), .Write_2(TTY_Wr_Controller_write_2));
  Multiplexer #(.select(2), .width(32), .disabled("Z"), .enable("false")) multiplexer_1 (
    .in0(bit_extender_1_out), .in1(bit_extender_2_out), .in2({32{1'b0}}), .in3({32{1'b0}}),
    .out(multiplexer_1_out), .sel(Address[3:2]));
  Comparator #(.width(2), .mode("unsigned")) comparator_12 (
    .a(Address[3:2]), .b(2'b00), .eq(comparator_12_eq));  // open: gt, lt
  Write_Align_Data KBD_Wr_Controller (
    .DataWr(WriteData), .DataPrev({32{1'b0}}), .SubAddr(Address[1:0]), .Mode(Mode), .Write(and_10_out),
    .DataOut(KBD_Wr_Controller_dataout), .Invalid(KBD_WINV), .Write_2(KBD_Wr_Controller_write_2));
  Write_Align_Data DISP_Wr_Controller (
    .DataWr(WriteData), .DataPrev({32{1'b0}}), .SubAddr(Address[1:0]), .Mode(Mode), .Write(and_9_out),
    .DataOut({DISP_Wr_Controller_dataout, DISP_WrData}), .Invalid(DISP_WINV),
    .Write_2(DISP_Wr_Controller_write_2));
  Write_Align_Data MTX_Wr_Controller (
    .DataWr(WriteData), .DataPrev({32{1'b0}}), .SubAddr(Address[1:0]), .Mode(Mode), .Write(and_11_out),
    .DataOut(MTX_WrData), .Invalid(MTX_WINV), .Write_2(MTX_Write));
  Multiplexer #(.select(1), .width(1), .disabled("Z"), .enable("false")) multiplexer_2 (
    .in0(TTY_Wr_Controller_write_2), .in1(1'b0), .out(TTY_Write), .sel(Address[2]));
  and and_12 (and_12_out, comparator_12_eq, KBD_SEL);
  Multiplexer #(.select(1), .width(1), .disabled("Z"), .enable("false")) multiplexer_3 (
    .in0(1'b0), .in1(TTY_Wr_Controller_write_2), .out(multiplexer_3_out), .sel(Address[2]));
  Read_Align_Data KBD_Rd_Controller (
    .DataIn(multiplexer_1_out), .SubAddr(Address[1:0]), .Mode(Mode), .SignExt(SignExt), .DataOut(KBD_RDOut),
    .Invalid(KBD_RINV));
  and and_13 (KBD_ReadEn, Read, and_12_out);
  and and_14 (KBD_Clear, KBD_Wr_Controller_dataout[0], KBD_Wr_Controller_write_2, CLK);
  Multiplexer #(.select(1), .width(1), .disabled("Z"), .enable("false")) multiplexer_4 (
    .in0(DISP_Wr_Controller_write_2), .in1(1'b0), .out(DISP_Write), .sel(Address[2]));
  Multiplexer #(.select(1), .width(1), .disabled("Z"), .enable("false")) multiplexer_5 (
    .in0(1'b0), .in1(DISP_Wr_Controller_write_2), .out(multiplexer_5_out), .sel(Address[2]));
  and and_15 (INV, controlled_buffer_1_out, or_6_out);
  or or_6 (or_6_out, Read, Write);
  and and_16 (TTY_Clear, TTY_WrData[0], multiplexer_3_out, CLK);
  and and_17 (DISP_Clear, DISP_WrData[0], multiplexer_5_out, CLK);

  assign MTX_WrAddr = Address[6:2];

  // Other names for the same wires on the sheet: SubAddr[1:0] = Address[1:0]; DISP_SubAddr[1:0] = Address[3:2];
  //   DISP_SubSel = Address[2]; HwAddr[11:0] = Address[13:2]; KBD_SubAddr[1:0] = Address[3:2];
  //   MTX_SubAddr[4:0] = Address[6:2]; TTY_SubAddr[1:0] = Address[3:2]; TTY_SubSel = Address[2];
  //   DISP_AINV = Address[3]; TTY_AINV = Address[3]; ChipSel[15:0] = Address[31:16]; WrData[31:0] = WriteData

  // Notes on the sheet:
  //   TTY
  //   KBD
  //   DISP
  //   Output
  //   MATRIX
  //   contents of FIRMWARE (hex, n*v repeats v):
  //   fe010113 812e23 2010413 100793 fef42623 793 78513 1c12403 2010113 8067
endmodule

module Read_Align_Data (
  input  [31:0] DataIn,
  input  [1:0] SubAddr,
  input  [1:0] Mode,
  input  SignExt,
  output [31:0] DataOut,
  output Invalid
);

  wire comparator_1_eq, not_1_out;
  wire [4:0] bit_extender_1_out, shifter_1_out;
  wire [31:0] bit_extender_2_out, bit_extender_3_out, bit_extender_4_out, bit_extender_5_out,
       multiplexer_2_out, multiplexer_3_out, shifter_2_out;

  assign bit_extender_1_out = {{3{1'b0}}, SubAddr};  // Bit_Extender bit_extender_1
  Shifter #(.width(5), .shift("ll")) shifter_1 (.in(bit_extender_1_out), .\dist (3'b011), .out(shifter_1_out));
  Comparator #(.width(2), .mode("unsigned")) comparator_1 (
    .a(SubAddr), .b(2'b00), .eq(comparator_1_eq));  // open: gt, lt
  not not_1 (not_1_out, comparator_1_eq);
  Shifter #(.width(32), .shift("lr")) shifter_2 (.in(DataIn), .\dist (shifter_1_out), .out(shifter_2_out));
  Multiplexer #(.select(2), .width(1), .disabled("Z"), .enable("false")) multiplexer_1 (
    .in0(1'b0), .in1(SubAddr[0]), .in2(not_1_out), .in3(1'b1), .out(Invalid), .sel(Mode));
  assign bit_extender_2_out = {{24{1'b0}}, shifter_2_out[7:0]};  // Bit_Extender bit_extender_2
  assign bit_extender_3_out = {{24{shifter_2_out[7]}}, shifter_2_out[7:0]};  // Bit_Extender bit_extender_3
  assign bit_extender_4_out = {{16{1'b0}}, shifter_2_out[15:0]};  // Bit_Extender bit_extender_4
  assign bit_extender_5_out = {{16{shifter_2_out[15]}}, shifter_2_out[15:0]};  // Bit_Extender bit_extender_5
  Multiplexer #(.select(2), .width(32), .disabled("Z"), .enable("false")) multiplexer_2 (
    .in0(bit_extender_2_out), .in1(bit_extender_4_out), .in2(shifter_2_out), .out(multiplexer_2_out),
    .sel(Mode));  // open: in3
  Multiplexer #(.select(2), .width(32), .disabled("Z"), .enable("false")) multiplexer_3 (
    .in0(bit_extender_3_out), .in1(bit_extender_5_out), .in2(shifter_2_out), .out(multiplexer_3_out),
    .sel(Mode));  // open: in3
  Multiplexer #(.select(1), .width(32), .disabled("Z"), .enable("false")) multiplexer_4 (
    .in0(multiplexer_2_out), .in1(multiplexer_3_out), .out(DataOut), .sel(SignExt));

  // Other names for the same wires on the sheet: SE = SignExt
endmodule

module Write_Align_Data (
  input  [31:0] DataWr,
  input  [31:0] DataPrev,
  input  [1:0] SubAddr,
  input  [1:0] Mode,
  input  Write,
  output [31:0] DataOut,
  output Invalid,
  output Write_2
);

  wire comparator_1_eq, not_1_out;
  wire [4:0] bit_extender_1_out, shifter_1_out;
  wire [31:0] and_2_out, bit_extender_2_out, bit_extender_3_out, bit_extender_4_out, bit_extender_5_out,
       multiplexer_1_out, multiplexer_3_out, not_2_out, shifter_2_out, shifter_3_out;

  assign bit_extender_1_out = {{3{1'b0}}, SubAddr};  // Bit_Extender bit_extender_1
  assign bit_extender_2_out = {{24{1'b0}}, DataWr[7:0]};  // Bit_Extender bit_extender_2
  assign bit_extender_3_out = {{16{1'b0}}, DataWr[15:0]};  // Bit_Extender bit_extender_3
  assign bit_extender_4_out = {{24{1'b0}}, {8{1'b1}}};  // Bit_Extender bit_extender_4
  assign bit_extender_5_out = {{16{1'b0}}, {16{1'b1}}};  // Bit_Extender bit_extender_5
  Shifter #(.width(5), .shift("ll")) shifter_1 (.in(bit_extender_1_out), .\dist (3'b011), .out(shifter_1_out));
  Comparator #(.width(2), .mode("unsigned")) comparator_1 (
    .a(SubAddr), .b(2'b00), .eq(comparator_1_eq));  // open: gt, lt
  not not_1 (not_1_out, comparator_1_eq);
  Multiplexer #(.select(2), .width(32), .disabled("Z"), .enable("false")) multiplexer_1 (
    .in0(bit_extender_2_out), .in1(bit_extender_3_out), .in2(DataWr), .out(multiplexer_1_out), .sel(Mode));  // open: in3
  Multiplexer #(.select(2), .width(1), .disabled("Z"), .enable("false")) multiplexer_2 (
    .in0(1'b0), .in1(SubAddr[0]), .in2(not_1_out), .in3(1'b1), .out(Invalid), .sel(Mode));
  Multiplexer #(.select(2), .width(32), .disabled("Z"), .enable("false")) multiplexer_3 (
    .in0(bit_extender_4_out), .in1(bit_extender_5_out), .in2({32{1'b1}}), .out(multiplexer_3_out), .sel(Mode));  // open: in3
  and and_1 (Write_2, ~Invalid, Write);  // AND_Gate
  Shifter #(.width(32), .shift("ll")) shifter_2 (.in(multiplexer_1_out), .\dist (shifter_1_out), .out(shifter_2_out));
  assign not_2_out = ~shifter_3_out;  // NOT_Gate not_2, 32 bits wide
  Shifter #(.width(32), .shift("ll")) shifter_3 (.in(multiplexer_3_out), .\dist (shifter_1_out), .out(shifter_3_out));
  assign and_2_out = DataPrev & not_2_out;  // AND_Gate and_2, 32 bits wide
  assign DataOut = shifter_2_out | and_2_out;  // OR_Gate or_1, 32 bits wide
endmodule

module test (
  input  [31:0] in_1,
  input  [31:0] in_2,
  input  in_3,
  input  in_4,
  input  [1:0] in_5,
  input  in_6,
  input  [6:0] in_7,
  input  in_8,
  output [31:0] out_9,
  output out_10,
  output out_11,
  output out_12,
  output out_13,
  output out_14,
  output [6:0] out_15,
  output out_16,
  output out_17
);

  wire clock_1_out, clock_2_out;
  wire [6:0] keyboard_1_data;
  wire [29:0] mmu_1_disp_wrdata;

  Clock #(.highDuration(1), .lowDuration(1)) clock_1 (.out(clock_1_out));
  Keyboard #(.Char_bit_width(7), .buflen(32), .trigger("rising")) keyboard_1 (
    .clk(clock_1_out), .data(keyboard_1_data));  // open: re, clr, avail
  TTY #(.Char_bit_width(7), .rows(8), .cols(32), .trigger("rising")) tty_1 (
    .data(keyboard_1_data), .clk(clock_1_out));  // open: we, clr
  Clock #(.highDuration(1), .lowDuration(1)) clock_2 (.out(clock_2_out));
  MMU mmu_1 (
    .Address(in_1), .WriteData(in_2), .Read(in_3), .Write(in_4), .Mode(in_5), .SignExt(in_6),
    .KBD_RdData(in_7), .KBD_AVAIL(in_8), .CLK(clock_2_out), .TTY_WrData(out_15), .TTY_Write(out_16),
    .TTY_Clear(out_17), .KBD_ReadEn(out_13), .KBD_Clear(out_14), .DISP_WrData(mmu_1_disp_wrdata),
    .DISP_Write(out_11), .DISP_Clear(out_12), .INV(out_10), .Out(out_9));  // open: MTX_WrData, MTX_Write, MTX_WrAddr
  // Probe on mmu_1_disp_wrdata
endmodule
