// Logisim project ALU.circ as structural Verilog: 16 circuits, main circuit ALU
module ALU (
  input  [31:0] X,
  input  [31:0] Y,
  input  CLK,
  input  Start,
  input  [5:0] ALUOP,
  output [5:0] Status,
  output Working,
  output [31:0] RES,
  output Invalid
);

  wire A_Invalid, A_Working, C_Invalid, C_Working, L_Invalid, L_Working, S_Invalid, S_Working;
  wire [1:0] FSTOP;
  wire [3:0] SECOP;
  wire [31:0] A_RES, C_RES, L_RES, S_RES;

  ALU_1_TO_2 alu_1_to_2_1 (.ALUOP(ALUOP), .OPER(SECOP), .TYPE(FSTOP));
  ARITH arith_1 (
    .X(X), .Y(Y), .CLK(CLK), .Start(Start), .SECONDARY_ALUOP(SECOP), .Working(A_Working), .RES(A_RES),
    .Invalid(A_Invalid));
  LOGIC logic_1 (
    .X(X), .Y(Y), .CLK(CLK), .Start(Start), .SECONDARY_ALUOP(SECOP), .Working(L_Working), .RES(L_RES),
    .Invalid(L_Invalid));
  COMPARE compare_1 (
    .X(X), .Y(Y), .CLK(CLK), .Start(Start), .SECONDARY_ALUOP(SECOP), .Working(C_Working), .RES(C_RES),
    .Invalid(C_Invalid));
  SYSTEM system_1 (
    .X(X), .Y(Y), .CLK(CLK), .Start(Start), .SECONDARY_ALUOP(SECOP), .Working(S_Working), .RES(S_RES),
    .Invalid(S_Invalid));
  COMPARE_STATUS compare_status_1 (.X(X), .Y(Y), .ALU_CMP_STAT(Status));
  Multiplexer #(.select(2), .width(1), .disabled("Z"), .enable("false")) multiplexer_1 (
    .in0(A_Working), .in1(L_Working), .in2(C_Working), .in3(S_Working), .out(Working), .sel(FSTOP));
  Multiplexer #(.select(2), .width(32), .disabled("Z"), .enable("false")) multiplexer_2 (
    .in0(A_RES), .in1(L_RES), .in2(C_RES), .in3(S_RES), .out(RES), .sel(FSTOP));
  Multiplexer #(.select(2), .width(1), .disabled("Z"), .enable("false")) multiplexer_3 (
    .in0(A_Invalid), .in1(L_Invalid), .in2(C_Invalid), .in3(S_Invalid), .out(Invalid), .sel(FSTOP));
endmodule

module ARITH (
  input  [31:0] X,
  input  [31:0] Y,
  input  CLK,
  input  Start,
  input  [3:0] SECONDARY_ALUOP,
  output Working,
  output [31:0] RES,
  output Invalid
);

  wire decoder_1_out0, decoder_1_out1, decoder_1_out2, decoder_1_out3, decoder_1_out4, decoder_1_out5,
       decoder_1_out6, decoder_1_out7, decoder_1_out8, decoder_1_out9, decoder_1_out10, decoder_1_out11,
       decoder_1_out12, decoder_1_out13, decoder_1_out14, decoder_1_out15;
  wire [31:0] adder_1_out, adder_2_out, mul_high_sig_and_unsig_1_out_3, mul_high_signed_1_out_3,
       multiplier_1_out, multiplier_2_cout, shifter_1_out, sign_div_1_q, sign_div_2_r, subtractor_1_out,
       usig_div_1_q, usig_div_2_r;

  Decoder #(.select(4), .tristate("false"), .disabled("Z"), .enable("false")) decoder_1 (
    .out0(decoder_1_out0), .out1(decoder_1_out1), .out2(decoder_1_out2), .out3(decoder_1_out3),
    .out4(decoder_1_out4), .out5(decoder_1_out5), .out6(decoder_1_out6), .out7(decoder_1_out7),
    .out8(decoder_1_out8), .out9(decoder_1_out9), .out10(decoder_1_out10), .out11(decoder_1_out11),
    .out12(decoder_1_out12), .out13(decoder_1_out13), .out14(decoder_1_out14), .out15(decoder_1_out15),
    .sel(SECONDARY_ALUOP));
  assign RES = Invalid ? {32{1'b0}} : 32'bz;  // Controlled_Buffer controlled_buffer_1
  or or_1 (Invalid, decoder_1_out15, decoder_1_out14, decoder_1_out13, decoder_1_out12, decoder_1_out11);
  Adder #(.width(32)) adder_1 (.a(X), .b(Y), .out(adder_1_out), .cin(1'b0));  // open: cout
  Subtractor #(.width(32)) subtractor_1 (.a(X), .b(Y), .out(subtractor_1_out), .bin(1'b0));  // open: bout
  Multiplier #(.width(32)) multiplier_1 (.a(X), .b(Y), .out(multiplier_1_out), .cin({32{1'b0}}));  // open: cout
  SIGN_DIV sign_div_1 (.X(X), .Y(Y), .Q(sign_div_1_q));  // open: R
  SIGN_DIV sign_div_2 (.X(X), .Y(Y), .R(sign_div_2_r));  // open: Q
  assign RES = decoder_1_out0 ? adder_1_out : 32'bz;  // Controlled_Buffer controlled_buffer_2
  assign RES = decoder_1_out1 ? subtractor_1_out : 32'bz;  // Controlled_Buffer controlled_buffer_3
  Adder #(.width(32)) adder_2 (.a(X), .b(shifter_1_out), .out(adder_2_out), .cin(1'b0));  // open: cout
  Shifter #(.width(32), .shift("ll")) shifter_1 (.in(Y), .\dist (5'b01100), .out(shifter_1_out));
  assign RES = decoder_1_out3 ? multiplier_1_out : 32'bz;  // Controlled_Buffer controlled_buffer_4
  MUL_HIGH_SIGNED mul_high_signed_1 (.X(X), .Y(Y), .out_3(mul_high_signed_1_out_3));
  assign RES = decoder_1_out4 ? mul_high_signed_1_out_3 : 32'bz;  // Controlled_Buffer controlled_buffer_5
  Multiplier #(.width(32)) multiplier_2 (.a(X), .b(Y), .cin({32{1'b0}}), .cout(multiplier_2_cout));  // open: out
  assign RES = decoder_1_out5 ? multiplier_2_cout : 32'bz;  // Controlled_Buffer controlled_buffer_6
  assign RES = decoder_1_out6 ? mul_high_sig_and_unsig_1_out_3 : 32'bz;  // Controlled_Buffer controlled_buffer_7
  MUL_HIGH_SIG_AND_UNSIG mul_high_sig_and_unsig_1 (.X(X), .Y(Y), .out_3(mul_high_sig_and_unsig_1_out_3));
  assign RES = decoder_1_out7 ? sign_div_1_q : 32'bz;  // Controlled_Buffer controlled_buffer_8
  assign RES = decoder_1_out8 ? usig_div_1_q : 32'bz;  // Controlled_Buffer controlled_buffer_9
  USIG_DIV usig_div_1 (.X(X), .Y(Y), .Q(usig_div_1_q));  // open: R
  assign RES = decoder_1_out9 ? sign_div_2_r : 32'bz;  // Controlled_Buffer controlled_buffer_10
  USIG_DIV usig_div_2 (.X(X), .Y(Y), .R(usig_div_2_r));  // open: Q
  assign RES = decoder_1_out10 ? usig_div_2_r : 32'bz;  // Controlled_Buffer controlled_buffer_11
  assign RES = decoder_1_out2 ? adder_2_out : 32'bz;  // Controlled_Buffer controlled_buffer_12

  assign Working = Start;

  // Notes on the sheet:
  //   0000 PLUS
  //   0001 MINUS
  //   0011 MUL_LOW
  //   0111 DIV_SIGNED
  //   1000 DIV_UNSIGNED
  //   1001 REM_SIGNED
  //   1010 REM_UNSIGNED
  //   0010 PLUS_AND_SHIFT12
  //   0100 MUL_HIGH_SIGNED
  //   0101 MUL_HIGH_UNSIGN
  //   0110 MUL_HIGH_SIG_UNSIG
  //   0000 PLUS
  //   0001 MINUS
  //   0011 MUL_LOW
  //   0111 DIV_SIGNED
  //   1000 DIV_UNSIGNED
  //   1001 REM_SIGNED
  //   1010 REM_UNSIGNED
  //   0010 PLUS_AND_SHIFT12
  //   0100 MUL_HIGH_SIGNED
  //   0101 MUL_HIGH_UNSIGN
  //   0110 MUL_HIGH_SIG_UNSIG
endmodule

module LOGIC (
  input  [31:0] X,
  input  [31:0] Y,
  input  CLK,
  input  Start,
  input  [3:0] SECONDARY_ALUOP,
  output Working,
  output [31:0] RES,
  output Invalid
);

  wire decoder_1_out0, decoder_1_out1, decoder_1_out2, decoder_1_out3, decoder_1_out4, decoder_1_out5,
       decoder_1_out6, decoder_1_out7;
  wire [31:0] and_1_out, or_2_out, RES_t, shifter_1_out, shifter_2_out, shifter_3_out, xor_1_out;

  Decoder #(.select(3), .tristate("false"), .disabled("Z"), .enable("false")) decoder_1 (
    .out0(decoder_1_out0), .out1(decoder_1_out1), .out2(decoder_1_out2), .out3(decoder_1_out3),
    .out4(decoder_1_out4), .out5(decoder_1_out5), .out6(decoder_1_out6), .out7(decoder_1_out7),
    .sel(SECONDARY_ALUOP[2:0]));
  Multiplexer #(.select(1), .width(32), .disabled("Z"), .enable("false")) multiplexer_1 (
    .in0(RES_t), .in1({32{1'b0}}), .out(RES), .sel(Invalid));
  or or_1 (Invalid, SECONDARY_ALUOP[3], decoder_1_out7, decoder_1_out6);
  assign and_1_out = X & Y;  // AND_Gate and_1, 32 bits wide
  assign or_2_out = X | Y;  // OR_Gate or_2, 32 bits wide
  assign RES_t = decoder_1_out0 ? and_1_out : 32'bz;  // Controlled_Buffer controlled_buffer_1
  assign RES_t = decoder_1_out1 ? or_2_out : 32'bz;  // Controlled_Buffer controlled_buffer_2
  assign RES_t = decoder_1_out2 ? xor_1_out : 32'bz;  // Controlled_Buffer controlled_buffer_3
  assign xor_1_out = X ^ Y;  // XOR_Gate xor_1, 32 bits wide
  Shifter #(.width(32), .shift("ll")) shifter_1 (.in(X), .\dist (Y[4:0]), .out(shifter_1_out));
  assign RES_t = decoder_1_out3 ? shifter_1_out : 32'bz;  // Controlled_Buffer controlled_buffer_4
  assign RES_t = decoder_1_out4 ? shifter_2_out : 32'bz;  // Controlled_Buffer controlled_buffer_5
  Shifter #(.width(32), .shift("lr")) shifter_2 (.in(X), .\dist (Y[4:0]), .out(shifter_2_out));
  assign RES_t = decoder_1_out5 ? shifter_3_out : 32'bz;  // Controlled_Buffer controlled_buffer_6
  Shifter #(.width(32), .shift("ar")) shifter_3 (.in(X), .\dist (Y[4:0]), .out(shifter_3_out));

  assign Working = Start;

  // Other names for the same wires on the sheet: ROUT[31:0] = RES

  // Notes on the sheet:
  //   0000 AND
  //   0001 OR
  //   0010 XOR
  //   0011 SHIFT_L
  //   0100 SHIFT_R_LOGICAL
  //   0101 SHIFT_R_ARITH
endmodule

module COMPARE (
  input  [31:0] X,
  input  [31:0] Y,
  input  CLK,
  input  Start,
  input  [3:0] SECONDARY_ALUOP,
  output Working,
  output [31:0] RES,
  output Invalid
);

  wire comparator_1_eq, comparator_2_lt, comparator_3_lt, decoder_1_out0, decoder_1_out1;
  wire [31:0] bit_extender_1_out, bit_extender_2_out, RES_t;

  Decoder #(.select(1), .tristate("false"), .disabled("Z"), .enable("false")) decoder_1 (
    .out0(decoder_1_out0), .out1(decoder_1_out1), .sel(SECONDARY_ALUOP[0]));
  not not_1 (Invalid, comparator_1_eq);
  Comparator #(.width(3), .mode("unsigned")) comparator_1 (
    .a(SECONDARY_ALUOP[3:1]), .b(3'b000), .eq(comparator_1_eq));  // open: gt, lt
  Multiplexer #(.select(1), .width(32), .disabled("Z"), .enable("false")) multiplexer_1 (
    .in0(RES_t), .in1({32{1'b0}}), .out(RES), .sel(Invalid));
  Comparator #(.width(32), .mode("twosComplement")) comparator_2 (.a(X), .b(Y), .lt(comparator_2_lt));  // open: gt, eq
  Comparator #(.width(32), .mode("unsigned")) comparator_3 (.a(X), .b(Y), .lt(comparator_3_lt));  // open: gt, eq
  assign bit_extender_1_out = {{31{1'b0}}, comparator_2_lt};  // Bit_Extender bit_extender_1
  assign bit_extender_2_out = {{31{1'b0}}, comparator_3_lt};  // Bit_Extender bit_extender_2
  assign RES_t = decoder_1_out0 ? bit_extender_1_out : 32'bz;  // Controlled_Buffer controlled_buffer_1
  assign RES_t = decoder_1_out1 ? bit_extender_2_out : 32'bz;  // Controlled_Buffer controlled_buffer_2

  assign Working = Start;

  // Other names for the same wires on the sheet: ROUT[31:0] = RES

  // Notes on the sheet:
  //   0000 SET_SIGN_LESS
  //   0001 SET_USIG_LESS
endmodule

module SYSTEM (
  input  [31:0] X,
  input  [31:0] Y,
  input  CLK,
  input  Start,
  input  [3:0] SECONDARY_ALUOP,
  output Working,
  output [31:0] RES,
  output Invalid
);

  wire comparator_1_eq;
  wire [31:0] RES_t;

  Comparator #(.width(4), .mode("unsigned")) comparator_1 (
    .a(SECONDARY_ALUOP), .b(4'b0000), .eq(comparator_1_eq));  // open: gt, lt
  not not_1 (Invalid, comparator_1_eq);
  Multiplexer #(.select(1), .width(32), .disabled("Z"), .enable("false")) multiplexer_1 (
    .in0(RES_t), .in1({32{1'b0}}), .out(RES), .sel(Invalid));
  assign RES_t = comparator_1_eq ? X : 32'bz;  // Controlled_Buffer controlled_buffer_1

  assign Working = Start;

  // Other names for the same wires on the sheet: ROUT[31:0] = RES

  // Notes on the sheet:
  //   0000 NOP
endmodule

module ALU_CMP_STATUS_DECODE (
  input  [5:0] STATUS_IN,
  output EQU,
  output NEQ,
  output SLT,
  output SGE,
  output ULT,
  output UGE
);


  assign EQU = STATUS_IN[0];
  assign NEQ = STATUS_IN[1];
  assign SGE = STATUS_IN[3];
  assign SLT = STATUS_IN[2];
  assign UGE = STATUS_IN[5];
  assign ULT = STATUS_IN[4];
endmodule

module COMPARE_STATUS (
  input  [31:0] X,
  input  [31:0] Y,
  output [5:0] ALU_CMP_STAT
);

  Comparator #(.width(32), .mode("twosComplement")) comparator_1 (
    .a(X), .b(Y), .eq(ALU_CMP_STAT[0]), .lt(ALU_CMP_STAT[2]));  // open: gt
  Comparator #(.width(32), .mode("unsigned")) comparator_2 (.a(X), .b(Y), .lt(ALU_CMP_STAT[4]));  // open: gt, eq
  not not_1 (ALU_CMP_STAT[1], ALU_CMP_STAT[0]);
  not not_2 (ALU_CMP_STAT[3], ALU_CMP_STAT[2]);
  not not_3 (ALU_CMP_STAT[5], ALU_CMP_STAT[4]);

  // Other names for the same wires on the sheet: EQUAL = ALU_CMP_STAT[0]; NOT_EQUAL = ALU_CMP_STAT[1];
  //   SIGNED_LESS = ALU_CMP_STAT[2]; SIGNED_GE = ALU_CMP_STAT[3]; UNSIG_LESS = ALU_CMP_STAT[4];
  //   UNSIG_GE = ALU_CMP_STAT[5]
endmodule

module ALU_6_TO_2 (
  input  _0,
  input  _1,
  input  _2,
  input  _3,
  input  _4,
  input  _5,
  output [3:0] OPER,
  output [1:0] TYPE
);


  assign OPER = {_3, _2, _1, _0};
  assign TYPE = {_5, _4};
endmodule

module ALU_6_TO_1 (
  input  _0,
  input  _1,
  input  _2,
  input  _3,
  input  _4,
  input  _5,
  output [5:0] ALUOP
);


  assign ALUOP = {_5, _4, _3, _2, _1, _0};
endmodule

module ALU_1_TO_2 (
  input  [5:0] ALUOP,
  output [3:0] OPER,
  output [1:0] TYPE
);


  assign OPER = ALUOP[3:0];
  assign TYPE = ALUOP[5:4];
endmodule

module MUL_HIGH_SIGNED (
  input  [31:0] X,
  input  [31:0] Y,
  output [31:0] out_3
);

  wire [31:0] multiplier_1_cout, multiplier_2_out, X1, Y1;

  assign X1 = {{31{X[31]}}, X[31]};  // Bit_Extender bit_extender_1
  assign Y1 = {{31{Y[31]}}, Y[31]};  // Bit_Extender bit_extender_2
  Multiplier #(.width(32)) multiplier_1 (.a(X), .b(Y), .cin({32{1'b0}}), .cout(multiplier_1_cout));  // open: out
  Multiplier #(.width(32)) multiplier_2 (.a(X1), .b(Y), .out(multiplier_2_out), .cin(multiplier_1_cout));  // open: cout
  Multiplier #(.width(32)) multiplier_3 (.a(X), .b(Y1), .out(out_3), .cin(multiplier_2_out));  // open: cout

  // Other names for the same wires on the sheet: X0[31:0] = X; Y0[31:0] = Y
endmodule

module MUL_HIGH_SIG_AND_UNSIG (
  input  [31:0] X,
  input  [31:0] Y,
  output [31:0] out_3
);

  wire [31:0] multiplier_1_cout, multiplier_2_out, X1;

  assign X1 = {{31{X[31]}}, X[31]};  // Bit_Extender bit_extender_1
  Multiplier #(.width(32)) multiplier_1 (.a(X), .b(Y), .cin({32{1'b0}}), .cout(multiplier_1_cout));  // open: out
  Multiplier #(.width(32)) multiplier_2 (.a(X1), .b(Y), .out(multiplier_2_out), .cin(multiplier_1_cout));  // open: cout
  Multiplier #(.width(32)) multiplier_3 (.a(X), .b({32{1'b0}}), .out(out_3), .cin(multiplier_2_out));  // open: cout

  // Other names for the same wires on the sheet: X0[31:0] = X; Y0[31:0] = Y
endmodule

module Absolute_Value (
  input  [31:0] X,
  output [31:0] VAL,
  output SGN
);

  wire [31:0] negator_1_out;

  Multiplexer #(.select(1), .width(32), .disabled("Z"), .enable("false")) multiplexer_1 (
    .in0(X), .in1(negator_1_out), .out(VAL), .sel(X[31]));
  Negator #(.width(32)) negator_1 (.in(X), .out(negator_1_out));

  assign SGN = X[31];
endmodule

module Sign_Mixer (
  input  [31:0] X,
  input  SGN,
  output [31:0] VAL
);

  wire [31:0] negator_1_out;

  Multiplexer #(.select(1), .width(32), .disabled("Z"), .enable("false")) multiplexer_1 (
    .in0(X), .in1(negator_1_out), .out(VAL), .sel(SGN));
  Negator #(.width(32)) negator_1 (.in(X), .out(negator_1_out));
endmodule

module SIGN_DIV (
  input  [31:0] X,
  input  [31:0] Y,
  output [31:0] Q,
  output [31:0] R
);

  wire absolute_value_1_sgn, absolute_value_2_sgn, comparator_1_eq, xor_1_out;
  wire [31:0] absolute_value_1_val, absolute_value_2_val, divider_1_out, divider_1_rem, Q1, R1;

  Absolute_Value absolute_value_1 (.X(X), .VAL(absolute_value_1_val), .SGN(absolute_value_1_sgn));
  Absolute_Value absolute_value_2 (.X(Y), .VAL(absolute_value_2_val), .SGN(absolute_value_2_sgn));
  Comparator #(.width(32), .mode("twosComplement")) comparator_1 (
    .a(Y), .b({32{1'b0}}), .eq(comparator_1_eq));  // open: gt, lt
  Sign_Mixer sign_mixer_1 (.X(divider_1_out), .SGN(xor_1_out), .VAL(Q1));
  Divider #(.width(32)) divider_1 (
    .a(absolute_value_1_val), .b(absolute_value_2_val), .out(divider_1_out), .rem(divider_1_rem));  // open: upper
  xor xor_1 (xor_1_out, absolute_value_1_sgn, absolute_value_2_sgn);
  Sign_Mixer sign_mixer_2 (.X(divider_1_rem), .SGN(absolute_value_1_sgn), .VAL(R1));
  Multiplexer #(.select(1), .width(32), .disabled("Z"), .enable("false")) multiplexer_1 (
    .in0(Q1), .in1({32{1'b1}}), .out(Q), .sel(comparator_1_eq));
  Multiplexer #(.select(1), .width(32), .disabled("Z"), .enable("false")) multiplexer_2 (
    .in0(R1), .in1(X), .out(R), .sel(comparator_1_eq));
endmodule

module USIG_DIV (
  input  [31:0] X,
  input  [31:0] Y,
  output [31:0] Q,
  output [31:0] R
);

  wire comparator_1_eq;
  wire [31:0] Q1, R1;

  Comparator #(.width(32), .mode("twosComplement")) comparator_1 (
    .a(Y), .b({32{1'b0}}), .eq(comparator_1_eq));  // open: gt, lt
  Divider #(.width(32)) divider_1 (.a(X), .b(Y), .out(Q1), .rem(R1));  // open: upper
  Multiplexer #(.select(1), .width(32), .disabled("Z"), .enable("false")) multiplexer_1 (
    .in0(Q1), .in1({32{1'b1}}), .out(Q), .sel(comparator_1_eq));
  Multiplexer #(.select(1), .width(32), .disabled("Z"), .enable("false")) multiplexer_2 (
    .in0(R1), .in1(X), .out(R), .sel(comparator_1_eq));
endmodule
