// Logisim project CSR.circ as structural Verilog: 3 circuits, main circuit CSR
module CSR_Interface (
  input  [31:0] SYNC_DATA,
  input  [11:0] SYNC_ADDR,
  input  SYNC_WRITE,
  input  [1:0] SYNC_OP,
  input  [31:0] MSTATUS_IN,
  input  [1:0] MSTATUS_OP,
  input  [31:0] MEPC_IN,
  input  [1:0] MEPC_OP,
  input  [31:0] MTVAL_IN,
  input  [1:0] MTVAL_OP,
  input  [31:0] MIP_IN,
  input  [1:0] MIP_OP,
  input  MCYCLE_CNTUP,
  input  MINSTRET_CNTUP,
  input  CLK,
  output [31:0] MSTATUS,
  output [31:0] MIE,
  output [31:0] MTVEC,
  output [31:0] MEPC,
  output [31:0] MTVAL,
  output [31:0] MIP,
  output [31:0] MCYCLE,
  output [31:0] MINSTRET,
  output SYNC_Invalid,
  output [31:0] SYNC_OUT
);

  wire IS_MCYCLE, IS_MEPC, IS_MIE, IS_MINSTRET, IS_MIP, IS_MSTATUS, IS_MTVAL, IS_MTVEC, multiplexer_1_out,
       multiplexer_2_out, multiplexer_3_out, multiplexer_4_out, multiplexer_5_out, multiplexer_6_out,
       multiplexer_7_out, multiplexer_8_out, not_1_out, or_1_out;

  Multiplexer #(.select(1), .width(1), .disabled("Z"), .enable("false")) multiplexer_1 (
    .in0(1'b0), .in1(SYNC_WRITE), .out(multiplexer_1_out), .sel(IS_MSTATUS));
  Comparator #(.width(12), .mode("unsigned")) comparator_1 (
    .a(SYNC_ADDR), .b(12'h300), .eq(IS_MSTATUS));  // open: gt, lt
  Multiplexer #(.select(1), .width(1), .disabled("Z"), .enable("false")) multiplexer_2 (
    .in0(1'b0), .in1(SYNC_WRITE), .out(multiplexer_2_out), .sel(IS_MIE));
  Comparator #(.width(12), .mode("unsigned")) comparator_2 (.a(SYNC_ADDR), .b(12'h304), .eq(IS_MIE));  // open: gt, lt
  Multiplexer #(.select(1), .width(1), .disabled("Z"), .enable("false")) multiplexer_3 (
    .in0(1'b0), .in1(SYNC_WRITE), .out(multiplexer_3_out), .sel(IS_MTVEC));
  Comparator #(.width(12), .mode("unsigned")) comparator_3 (.a(SYNC_ADDR), .b(12'h305), .eq(IS_MTVEC));  // open: gt, lt
  Multiplexer #(.select(1), .width(1), .disabled("Z"), .enable("false")) multiplexer_4 (
    .in0(1'b0), .in1(SYNC_WRITE), .out(multiplexer_4_out), .sel(IS_MEPC));
  Comparator #(.width(12), .mode("unsigned")) comparator_4 (.a(SYNC_ADDR), .b(12'h341), .eq(IS_MEPC));  // open: gt, lt
  Multiplexer #(.select(1), .width(1), .disabled("Z"), .enable("false")) multiplexer_5 (
    .in0(1'b0), .in1(SYNC_WRITE), .out(multiplexer_5_out), .sel(IS_MTVAL));
  Comparator #(.width(12), .mode("unsigned")) comparator_5 (.a(SYNC_ADDR), .b(12'h343), .eq(IS_MTVAL));  // open: gt, lt
  Multiplexer #(.select(1), .width(1), .disabled("Z"), .enable("false")) multiplexer_6 (
    .in0(1'b0), .in1(SYNC_WRITE), .out(multiplexer_6_out), .sel(IS_MIP));
  Comparator #(.width(12), .mode("unsigned")) comparator_6 (.a(SYNC_ADDR), .b(12'h344), .eq(IS_MIP));  // open: gt, lt
  Multiplexer #(.select(1), .width(1), .disabled("Z"), .enable("false")) multiplexer_7 (
    .in0(1'b0), .in1(SYNC_WRITE), .out(multiplexer_7_out), .sel(IS_MCYCLE));
  Comparator #(.width(12), .mode("unsigned")) comparator_7 (
    .a(SYNC_ADDR), .b(12'hb00), .eq(IS_MCYCLE));  // open: gt, lt
  Multiplexer #(.select(1), .width(1), .disabled("Z"), .enable("false")) multiplexer_8 (
    .in0(1'b0), .in1(SYNC_WRITE), .out(multiplexer_8_out), .sel(IS_MINSTRET));
  Comparator #(.width(12), .mode("unsigned")) comparator_8 (
    .a(SYNC_ADDR), .b(12'hb02), .eq(IS_MINSTRET));  // open: gt, lt
  CSR _300_MSTATUS (
    .ASYNC_DATA(MSTATUS_IN), .SYNC_DATA(SYNC_DATA), .SYNC_OP(SYNC_OP), .CLK(CLK),
    .SYNC_WRITE(multiplexer_1_out), .MASK({32{1'b0}}), .ASYNC_OP(MSTATUS_OP), .COUNTUP(1'b0), .OUT(MSTATUS));
  CSR _304_MIE (
    .ASYNC_DATA({32{1'b0}}), .SYNC_DATA(SYNC_DATA), .SYNC_OP(SYNC_OP), .CLK(CLK),
    .SYNC_WRITE(multiplexer_2_out), .MASK(32'h8), .ASYNC_OP(2'b00), .COUNTUP(1'b0), .OUT(MIE));
  CSR _305_MTVEC (
    .ASYNC_DATA({32{1'b0}}), .SYNC_DATA(SYNC_DATA), .SYNC_OP(SYNC_OP), .CLK(CLK),
    .SYNC_WRITE(multiplexer_3_out), .MASK({32{1'b0}}), .ASYNC_OP(2'b00), .COUNTUP(1'b0), .OUT(MTVEC));
  CSR _341_MEPC (
    .ASYNC_DATA(MEPC_IN), .SYNC_DATA(SYNC_DATA), .SYNC_OP(SYNC_OP), .CLK(CLK),
    .SYNC_WRITE(multiplexer_4_out), .MASK({32{1'b0}}), .ASYNC_OP(MEPC_OP), .COUNTUP(1'b0), .OUT(MEPC));
  CSR _343_MTVAL (
    .ASYNC_DATA(MTVAL_IN), .SYNC_DATA(SYNC_DATA), .SYNC_OP(SYNC_OP), .CLK(CLK),
    .SYNC_WRITE(multiplexer_5_out), .MASK({32{1'b0}}), .ASYNC_OP(MTVAL_OP), .COUNTUP(1'b0), .OUT(MTVAL));
  CSR _344_MIP (
    .ASYNC_DATA(MIP_IN), .SYNC_DATA(SYNC_DATA), .SYNC_OP(SYNC_OP), .CLK(CLK), .SYNC_WRITE(multiplexer_6_out),
    .MASK({32{1'b0}}), .ASYNC_OP(MIP_OP), .COUNTUP(1'b0), .OUT(MIP));
  CSR B00_MCYCLE (
    .ASYNC_DATA({32{1'b0}}), .SYNC_DATA(SYNC_DATA), .SYNC_OP(SYNC_OP), .CLK(CLK),
    .SYNC_WRITE(multiplexer_7_out), .MASK({32{1'b0}}), .ASYNC_OP(2'b00), .COUNTUP(MCYCLE_CNTUP), .OUT(MCYCLE));
  CSR B02_MINSTRET (
    .ASYNC_DATA({32{1'b0}}), .SYNC_DATA(SYNC_DATA), .SYNC_OP(SYNC_OP), .CLK(CLK),
    .SYNC_WRITE(multiplexer_8_out), .MASK({32{1'b0}}), .ASYNC_OP(2'b00), .COUNTUP(MINSTRET_CNTUP),
    .OUT(MINSTRET));
  not not_1 (not_1_out, or_1_out);
  or or_1 (or_1_out, IS_MSTATUS, IS_MIE, IS_MTVEC, IS_MEPC, IS_MTVAL, IS_MIP, IS_MCYCLE, IS_MINSTRET);
  assign SYNC_OUT = not_1_out ? {32{1'b0}} : 32'bz;  // Controlled_Buffer controlled_buffer_1
  assign SYNC_OUT = IS_MSTATUS ? MSTATUS : 32'bz;  // Controlled_Buffer controlled_buffer_2
  assign SYNC_OUT = IS_MIE ? MIE : 32'bz;  // Controlled_Buffer controlled_buffer_3
  assign SYNC_OUT = IS_MTVEC ? MTVEC : 32'bz;  // Controlled_Buffer controlled_buffer_4
  assign SYNC_OUT = IS_MEPC ? MEPC : 32'bz;  // Controlled_Buffer controlled_buffer_5
  assign SYNC_OUT = IS_MTVAL ? MTVAL : 32'bz;  // Controlled_Buffer controlled_buffer_6
  assign SYNC_OUT = IS_MIP ? MIP : 32'bz;  // Controlled_Buffer controlled_buffer_7
  assign SYNC_OUT = IS_MCYCLE ? MCYCLE : 32'bz;  // Controlled_Buffer controlled_buffer_8
  assign SYNC_OUT = IS_MINSTRET ? MINSTRET : 32'bz;  // Controlled_Buffer controlled_buffer_9
  and and_1 (SYNC_Invalid, not_1_out, SYNC_WRITE);

  // Other names for the same wires on the sheet: Invalid = SYNC_Invalid
endmodule

module CSR (
  input  [31:0] ASYNC_DATA,
  input  [1:0] ASYNC_OP,
  input  [31:0] SYNC_DATA,
  input  [1:0] SYNC_OP,
  input  SYNC_WRITE,
  input  COUNTUP,
  input  [31:0] MASK,
  input  CLK,
  output [31:0] OUT
);

  wire ASYNC_DO_OPERATION, or_3_out;
  wire [31:0] and_1_out, and_2_out, ASYNC_WriteData, COUNTUP_WriteData, multiplexer_3_out, multiplexer_4_out,
       multiplexer_5_out, or_1_out, or_2_out, register_1_q, SYNC_WriteData;

  Adder #(.width(32)) adder_1 (.a(OUT), .b(32'h1), .out(COUNTUP_WriteData), .cin(1'b0));  // open: cout
  assign or_1_out = ASYNC_DATA | OUT;  // OR_Gate or_1, 32 bits wide
  assign and_1_out = ~ASYNC_DATA & OUT;  // AND_Gate and_1, 32 bits wide
  BitFinder #(.width(2), .\type ("low1")) bitfinder_1 (.in(ASYNC_OP), .found(ASYNC_DO_OPERATION));  // open: index
  assign or_2_out = SYNC_DATA | OUT;  // OR_Gate or_2, 32 bits wide
  assign and_2_out = ~SYNC_DATA & OUT;  // AND_Gate and_2, 32 bits wide
  Multiplexer #(.select(2), .width(32), .disabled("Z"), .enable("false")) multiplexer_1 (
    .in0({32{1'b0}}), .in1(ASYNC_DATA), .in2(or_1_out), .in3(and_1_out), .out(ASYNC_WriteData), .sel(ASYNC_OP));
  Multiplexer #(.select(2), .width(32), .disabled("Z"), .enable("false")) multiplexer_2 (
    .in0(OUT), .in1(SYNC_DATA), .in2(or_2_out), .in3(and_2_out), .out(SYNC_WriteData), .sel(SYNC_OP));
  Multiplexer #(.select(1), .width(32), .disabled("Z"), .enable("false")) multiplexer_3 (
    .in0({32{1'b0}}), .in1(COUNTUP_WriteData), .out(multiplexer_3_out), .sel(COUNTUP));
  Multiplexer #(.select(1), .width(32), .disabled("Z"), .enable("false")) multiplexer_4 (
    .in0(multiplexer_3_out), .in1(SYNC_WriteData), .out(multiplexer_4_out), .sel(SYNC_WRITE));
  or or_3 (or_3_out, ASYNC_DO_OPERATION, SYNC_WRITE, COUNTUP);
  Multiplexer #(.select(1), .width(32), .disabled("Z"), .enable("false")) multiplexer_5 (
    .in0(multiplexer_4_out), .in1(ASYNC_WriteData), .out(multiplexer_5_out), .sel(ASYNC_DO_OPERATION));
  Register #(.width(32), .trigger("falling"), .Select("low")) register_1 (
    .D(multiplexer_5_out), .en(or_3_out), .Q(register_1_q), .clk(CLK), .clr(1'b0), .cs(1'b0), .preset(1'b0));
  assign OUT = register_1_q | MASK;  // OR_Gate or_4, 32 bits wide

  // Other names for the same wires on the sheet: COUNTUP_DO_OPERATION = COUNTUP; Output[31:0] = OUT;
  //   SYNC_DO_OPERATION = SYNC_WRITE
endmodule

module test (
  input  [31:0] in_1,
  input  [1:0] in_2,
  input  [31:0] in_3,
  input  [1:0] in_4,
  input  in_5,
  input  [31:0] in_6,
  input  [11:0] in_7,
  input  [31:0] in_8,
  input  [31:0] in_9,
  input  [31:0] in_10,
  input  [31:0] in_11,
  input  [1:0] in_12,
  input  [1:0] in_13,
  input  [1:0] in_14,
  input  [1:0] in_15,
  input  in_16,
  input  [1:0] in_17
);

  wire clock_1_out, clock_2_out, csr_interface_1_sync_invalid;
  wire [31:0] csr_1_out, csr_interface_1_mcycle, csr_interface_1_mepc, csr_interface_1_mie,
       csr_interface_1_minstret, csr_interface_1_mip, csr_interface_1_mstatus, csr_interface_1_mtval,
       csr_interface_1_mtvec, csr_interface_1_sync_out;

  Clock #(.highDuration(1), .lowDuration(1)) clock_1 (.out(clock_1_out));
  Clock #(.highDuration(1), .lowDuration(1)) clock_2 (.out(clock_2_out));
  CSR csr_1 (
    .ASYNC_DATA(in_1), .SYNC_DATA(in_3), .SYNC_OP(in_4), .CLK(clock_1_out), .SYNC_WRITE(in_5),
    .MASK({32{1'b0}}), .ASYNC_OP(in_2), .COUNTUP(clock_1_out), .OUT(csr_1_out));
  // Probe on csr_interface_1_sync_invalid
  // Probe on csr_interface_1_sync_out
  // Probe on csr_1_out
  // Probe on csr_interface_1_mstatus
  // Probe on csr_interface_1_mie
  // Probe on csr_interface_1_mtvec
  // Probe on csr_interface_1_mepc
  CSR_Interface csr_interface_1 (
    .SYNC_DATA(in_6), .SYNC_ADDR(in_7), .SYNC_WRITE(in_16), .SYNC_OP(in_17), .MSTATUS_IN(in_8),
    .MSTATUS_OP(in_12), .MEPC_IN(in_9), .MEPC_OP(in_13), .MTVAL_IN(in_10), .MTVAL_OP(in_14), .MIP_IN(in_11),
    .MIP_OP(in_15), .MCYCLE_CNTUP(clock_2_out), .MINSTRET_CNTUP(clock_2_out), .CLK(clock_2_out),
    .MSTATUS(csr_interface_1_mstatus), .MIE(csr_interface_1_mie), .MTVEC(csr_interface_1_mtvec),
    .MEPC(csr_interface_1_mepc), .MTVAL(csr_interface_1_mtval), .MIP(csr_interface_1_mip),
    .MCYCLE(csr_interface_1_mcycle), .MINSTRET(csr_interface_1_minstret),
    .SYNC_Invalid(csr_interface_1_sync_invalid), .SYNC_OUT(csr_interface_1_sync_out));
  // Probe on csr_interface_1_mtval
  // Probe on csr_interface_1_mip
  // Probe on csr_interface_1_mcycle
  // Probe on csr_interface_1_minstret
endmodule
