// Logisim project DECODER.circ as structural Verilog: 8 circuits, main circuit DECODER
module DECODER (
  input  [31:0] INSTR,
  input  [5:0] ALU_COMP_STATUS,
  output [24:0] BasicControl,
  output [12:0] FloatControl,
  output [6:0] CSRControl,
  output [31:0] Immed,
  output [4:0] RS1,
  output [4:0] RS2,
  output [4:0] RD,
  output [4:0] FLOAT_FRS3,
  output [1:0] FLOAT_RM
);

  wire comparator_1_eq, comparator_2_eq, comparator_3_eq, comparator_4_eq, decoder_1_out0, decoder_1_out4,
       decoder_1_out5, decoder_1_out8, decoder_1_out12, decoder_1_out13, decoder_1_out24, decoder_1_out25,
       decoder_1_out27, decoder_1_out28, multiplexer_2_out;
  wire [3:3] not_1_out, or_1_out;
  wire [6:0] multiplexer_6_out, multiplexer_7_out, rom_7_data, undriven;
  wire [10:10] multiplexer_1_out;
  wire [24:0] multiplexer_3_out, multiplexer_4_out, multiplexer_5_out, rom_1_data, rom_2_data, rom_3_data,
       rom_4_data, rom_5_data, rom_6_data;
  wire [31:0] B_IMM, I_IMM, J_IMM, S_IMM;

  assign I_IMM = {{20{INSTR[31]}}, INSTR[31:20]};  // Bit_Extender bit_extender_1
  assign S_IMM = {{20{INSTR[31]}}, {INSTR[31:25], INSTR[11:7]}};  // Bit_Extender bit_extender_2
  assign B_IMM = {{20{INSTR[31]}}, {INSTR[31], INSTR[7], INSTR[30:25], INSTR[11:8]}};  // Bit_Extender bit_extender_3
  assign J_IMM = {{12{INSTR[31]}}, {INSTR[31], INSTR[19:12], INSTR[20], INSTR[30:21]}};  // Bit_Extender bit_extender_4
  Decoder #(.select(5), .tristate("false"), .disabled("Z"), .enable("false")) decoder_1 (
    .out0(decoder_1_out0), .out4(decoder_1_out4), .out5(decoder_1_out5), .out8(decoder_1_out8),
    .out12(decoder_1_out12), .out13(decoder_1_out13), .out24(decoder_1_out24), .out25(decoder_1_out25),
    .out27(decoder_1_out27), .out28(decoder_1_out28), .sel(INSTR[6:2]));  // open: out1, out2, out3, out6, out7, out9, out10, out11, out14, out15, out16, out17, out18, out19, out20, out21, out22, out23, out26, out29, out30, out31
  assign Immed = decoder_1_out0 ? I_IMM : 32'bz;  // Controlled_Buffer controlled_buffer_1
  assign Immed = decoder_1_out4 ? I_IMM : 32'bz;  // Controlled_Buffer controlled_buffer_2
  assign Immed = decoder_1_out5 ? {{12{1'b0}}, INSTR[31:12]} : 32'bz;  // Controlled_Buffer controlled_buffer_3
  assign Immed = decoder_1_out8 ? S_IMM : 32'bz;  // Controlled_Buffer controlled_buffer_4
  assign Immed = decoder_1_out12 ? {32{1'b0}} : 32'bz;  // Controlled_Buffer controlled_buffer_5
  assign Immed = decoder_1_out13 ? {{12{1'b0}}, INSTR[31:12]} : 32'bz;  // Controlled_Buffer controlled_buffer_6
  assign Immed = decoder_1_out24 ? B_IMM : 32'bz;  // Controlled_Buffer controlled_buffer_7
  assign Immed = decoder_1_out25 ? I_IMM : 32'bz;  // Controlled_Buffer controlled_buffer_8
  assign Immed = decoder_1_out27 ? J_IMM : 32'bz;  // Controlled_Buffer controlled_buffer_9
  assign Immed = decoder_1_out28 ? I_IMM : 32'bz;  // Controlled_Buffer controlled_buffer_10
  Comparator #(.width(3), .mode("unsigned")) comparator_1 (
    .a(INSTR[14:12]), .b(3'b101), .eq(comparator_1_eq));  // open: gt, lt
  assign BasicControl = decoder_1_out5 ? 25'h32217 : 25'bz;  // Controlled_Buffer controlled_buffer_11
  assign CSRControl = decoder_1_out5 ? {7{1'b0}} : 7'bz;  // Controlled_Buffer controlled_buffer_12
  assign BasicControl = decoder_1_out13 ? 25'h32216 : 25'bz;  // Controlled_Buffer controlled_buffer_13
  assign CSRControl = decoder_1_out13 ? {7{1'b0}} : 7'bz;  // Controlled_Buffer controlled_buffer_14
  Multiplexer #(.select(3), .width(1), .disabled("Z"), .enable("false")) multiplexer_1 (
    .in0(ALU_COMP_STATUS[0]), .in1(ALU_COMP_STATUS[1]), .in2(1'b0), .in3(1'b0), .in4(ALU_COMP_STATUS[2]),
    .in5(ALU_COMP_STATUS[3]), .in6(ALU_COMP_STATUS[4]), .in7(ALU_COMP_STATUS[5]),
    .out(multiplexer_1_out[10]), .sel(INSTR[14:12]));
  assign CSRControl = decoder_1_out24 ? undriven : 7'bz;  // Controlled_Buffer controlled_buffer_15
  assign BasicControl = decoder_1_out25 ? 25'h32f81 : 25'bz;  // Controlled_Buffer controlled_buffer_16
  assign CSRControl = decoder_1_out25 ? {7{1'b0}} : 7'bz;  // Controlled_Buffer controlled_buffer_17
  assign BasicControl = decoder_1_out27 ? 25'h32b81 : 25'bz;  // Controlled_Buffer controlled_buffer_18
  assign CSRControl = decoder_1_out27 ? {7{1'b0}} : 7'bz;  // Controlled_Buffer controlled_buffer_19
  ROM #(.addrWidth(3), .dataWidth(25), .Select("low")) rom_1 (.addr(INSTR[14:12]), .data(rom_1_data));
  or or_1 (or_1_out[3], rom_2_data[3], multiplexer_2_out);
  ROM #(.addrWidth(3), .dataWidth(25), .Select("low")) rom_2 (.addr(INSTR[14:12]), .data(rom_2_data));
  Multiplexer #(.select(1), .width(1), .disabled("Z"), .enable("false")) multiplexer_2 (
    .in0(1'b0), .in1(I_IMM[10]), .out(multiplexer_2_out), .sel(comparator_1_eq));
  assign BasicControl = decoder_1_out8 ? rom_3_data : 25'bz;  // Controlled_Buffer controlled_buffer_20
  ROM #(.addrWidth(3), .dataWidth(25), .Select("low")) rom_3 (.addr(INSTR[14:12]), .data(rom_3_data));
  assign CSRControl = decoder_1_out8 ? {7{1'b0}} : 7'bz;  // Controlled_Buffer controlled_buffer_21
  ROM #(.addrWidth(3), .dataWidth(25), .Select("low")) rom_4 (.addr(INSTR[14:12]), .data(rom_4_data));
  ROM #(.addrWidth(3), .dataWidth(25), .Select("low")) rom_5 (.addr(INSTR[14:12]), .data(rom_5_data));
  ROM #(.addrWidth(3), .dataWidth(25), .Select("low")) rom_6 (.addr(INSTR[14:12]), .data(rom_6_data));
  Multiplexer #(.select(2), .width(25), .disabled("Z"), .enable("false")) multiplexer_3 (
    .in0(25'h12380), .in1(25'h12380), .in2(25'h13380), .in3({25{1'b0}}), .out(multiplexer_3_out),
    .sel(I_IMM[1:0]));
  Comparator #(.width(3), .mode("unsigned")) comparator_2 (
    .a(INSTR[14:12]), .b(3'b000), .eq(comparator_2_eq));  // open: gt, lt
  ROM #(.addrWidth(3), .dataWidth(7), .Select("low")) rom_7 (.addr(INSTR[14:12]), .data(rom_7_data));
  Comparator #(.width(3), .mode("unsigned")) comparator_3 (
    .a(INSTR[14:12]), .b(3'b000), .eq(comparator_3_eq));  // open: gt, lt
  assign BasicControl = decoder_1_out0 ? rom_1_data : 25'bz;  // Controlled_Buffer controlled_buffer_22
  assign CSRControl = decoder_1_out0 ? {7{1'b0}} : 7'bz;  // Controlled_Buffer controlled_buffer_23
  assign BasicControl = decoder_1_out4 ? {rom_2_data[24:4], or_1_out[3], rom_2_data[2:0]} : 25'bz;  // Controlled_Buffer controlled_buffer_24
  assign CSRControl = decoder_1_out4 ? {7{1'b0}} : 7'bz;  // Controlled_Buffer controlled_buffer_25
  Multiplexer #(.select(2), .width(25), .disabled("Z"), .enable("false")) multiplexer_4 (
    .in0(rom_4_data), .in1(rom_5_data), .in2(rom_6_data), .out(multiplexer_4_out),
    .sel({INSTR[30], INSTR[25]}));  // open: in3
  assign CSRControl = decoder_1_out12 ? {7{1'b0}} : 7'bz;  // Controlled_Buffer controlled_buffer_26
  assign BasicControl = decoder_1_out24 ? {14'h24, multiplexer_1_out[10], 10'h380} : 25'bz;  // Controlled_Buffer controlled_buffer_27
  Multiplexer #(.select(1), .width(25), .disabled("Z"), .enable("false")) multiplexer_5 (
    .in0(25'h3e380), .in1(multiplexer_3_out), .out(multiplexer_5_out), .sel(comparator_2_eq));
  Comparator #(.width(5), .mode("unsigned")) comparator_4 (
    .a(INSTR[19:15]), .b({5{1'b0}}), .eq(comparator_4_eq));  // open: gt, lt
  Multiplexer #(.select(2), .width(7), .disabled("Z"), .enable("false")) multiplexer_6 (
    .in0(7'b0010000), .in1(7'b0100000), .in2(7'b1000000), .in3({7{1'b0}}), .out(multiplexer_6_out),
    .sel(I_IMM[1:0]));
  assign BasicControl = decoder_1_out12 ? multiplexer_4_out : 25'bz;  // Controlled_Buffer controlled_buffer_28
  not not_1 (not_1_out[3], comparator_4_eq);
  assign BasicControl = decoder_1_out28 ? multiplexer_5_out : 25'bz;  // Controlled_Buffer controlled_buffer_29
  assign CSRControl = decoder_1_out28 ? multiplexer_7_out : 7'bz;  // Controlled_Buffer controlled_buffer_30
  Multiplexer #(.select(1), .width(7), .disabled("Z"), .enable("false")) multiplexer_7 (
    .in0({rom_7_data[6:4], not_1_out[3], rom_7_data[2:0]}), .in1(multiplexer_6_out), .out(multiplexer_7_out),
    .sel(comparator_3_eq));

  assign FLOAT_FRS3 = {5{1'b0}};
  assign FLOAT_RM = 2'b00;
  assign FloatControl = {13{1'b0}};
  assign RD = INSTR[11:7];
  assign RS1 = INSTR[19:15];
  assign RS2 = INSTR[24:20];

  // Other names for the same wires on the sheet: U_IMM[19:0] = INSTR[31:12]; FUNCT7[6:0] = INSTR[31:25];
  //   FUNCT3[2:0] = INSTR[14:12]; A_S[5:0] = ALU_COMP_STATUS; BC_BUS[24:0] = BasicControl; CSR_BUS[6:0] = CSRControl;
  //   IMM_LOW2[1:0] = I_IMM[1:0]; IMM_BUS[31:0] = Immed; OPCODE[6:0] = INSTR[6:0]

  // Notes on the sheet:
  //   R-TYPE
  //   I-TYPE
  //   S-TYPE
  //   B-TYPE, do NOT SHL
  //   U-TYPE
  //   J-TYPE, do NOT SHL
  //   [00000][11] LOAD
  //   [00100][11] ImmArith
  //   [00101][11] AUIPC
  //   [01000][11] STORE
  //   [01100][11] RegArith
  //   [01101][11] LUI
  //   [11000][11] Bcc
  //   [11001][11] JALR
  //   [11011][11] JAL
  //   [11100][11] Exception
  //   contents of rom_1 (hex, n*v repeats v):
  //   1136204 1536204 1936204 0 136204 536204
  //   contents of rom_2 (hex, n*v repeats v):
  //   32204 3229c 32304 3230c 32294 322a4 3228c 32284
  //   contents of rom_3 (hex, n*v repeats v):
  //   212204 612204 a12204
  //   contents of rom_4 (hex, n*v repeats v):
  //   32200 32298 32300 32308 32290 322a0 32288 32280
  //   contents of rom_5 (hex, n*v repeats v):
  //   32218 32220 32230 32228 32238 32240 32248 32250
  //   contents of rom_6 (hex, n*v repeats v):
  //   32208 4*0 322a8
  //   contents of rom_7 (hex, n*v repeats v):
  //   0 2 4 6 0 b d f
endmodule

module Basic_ControlBits_MUX (
  input  [1:0] ALU_X_DATAFROM,
  input  ALU_Y_DATAFROM,
  input  [5:0] ALU_OP,
  input  ALU_CALC,
  input  [2:0] PC_DATAFROM,
  input  PC_WRITE,
  input  [1:0] REG_DATAFROM,
  input  REG_READ,
  input  REG_WRITE,
  input  MEM_ADDRFROM,
  input  MEM_DATAFROM,
  input  MEM_READ,
  input  MEM_WRITE,
  input  [1:0] MEM_MODE,
  input  MEM_SIGNEXT,
  output [24:0] Basic_ControlBits
);


  assign Basic_ControlBits = {MEM_SIGNEXT, MEM_MODE, MEM_WRITE, MEM_READ, MEM_DATAFROM, MEM_ADDRFROM, REG_WRITE, REG_READ, REG_DATAFROM, PC_WRITE, PC_DATAFROM, ALU_CALC, ALU_OP, ALU_Y_DATAFROM, ALU_X_DATAFROM};
endmodule

module Basic_ControlBits_DMX (
  input  [24:0] Basic_ControlBits,
  output [1:0] ALU_X_DATAFROM,
  output ALU_Y_DATAFROM,
  output [5:0] ALU_OP,
  output ALU_CALC,
  output [2:0] PC_DATAFROM,
  output PC_WRITE,
  output [1:0] REG_DATAFROM,
  output REG_READ,
  output REG_WRITE,
  output MEM_ADDRFROM,
  output MEM_DATAFROM,
  output MEM_READ,
  output MEM_WRITE,
  output [1:0] MEM_MODE,
  output MEM_SIGNEXT
);


  assign ALU_CALC = Basic_ControlBits[9];
  assign ALU_OP = Basic_ControlBits[8:3];
  assign ALU_X_DATAFROM = Basic_ControlBits[1:0];
  assign ALU_Y_DATAFROM = Basic_ControlBits[2];
  assign MEM_ADDRFROM = Basic_ControlBits[18];
  assign MEM_DATAFROM = Basic_ControlBits[19];
  assign MEM_MODE = Basic_ControlBits[23:22];
  assign MEM_READ = Basic_ControlBits[20];
  assign MEM_SIGNEXT = Basic_ControlBits[24];
  assign MEM_WRITE = Basic_ControlBits[21];
  assign PC_DATAFROM = Basic_ControlBits[12:10];
  assign PC_WRITE = Basic_ControlBits[13];
  assign REG_DATAFROM = Basic_ControlBits[15:14];
  assign REG_READ = Basic_ControlBits[16];
  assign REG_WRITE = Basic_ControlBits[17];
endmodule

module Floating_ControlBits_MUX (
  input  [1:0] FLREG_DATAFROM,
  input  FLREG_READ,
  input  FLREG_WRITE,
  input  FPU_X_DATAFROM,
  input  [6:0] FPU_OP,
  input  FPU_CALC,
  output [12:0] Floating_ControlBits
);


  assign Floating_ControlBits = {FPU_CALC, FPU_OP, FPU_X_DATAFROM, FLREG_WRITE, FLREG_READ, FLREG_DATAFROM};
endmodule

module Floating_ControlBits_DMX (
  input  [12:0] Floating_ControlBits,
  output [1:0] FLREG_DATAFROM,
  output FLREG_READ,
  output FLREG_WRITE,
  output FPU_X_DATAFROM,
  output [6:0] FPU_OP,
  output FPU_CALC
);


  assign FLREG_DATAFROM = Floating_ControlBits[1:0];
  assign FLREG_READ = Floating_ControlBits[2];
  assign FLREG_WRITE = Floating_ControlBits[3];
  assign FPU_CALC = Floating_ControlBits[12];
  assign FPU_OP = Floating_ControlBits[11:5];
  assign FPU_X_DATAFROM = Floating_ControlBits[4];
endmodule

module CSR_MUX (
  input  CSR_DATAFROM,
  input  [1:0] CSR_OP,
  input  CSR_WRITE,
  input  TRAP_ECALL,
  input  TRAP_EBREAK,
  input  TRAP_MRET,
  output [6:0] out_7
);


  assign out_7 = {TRAP_MRET, TRAP_EBREAK, TRAP_ECALL, CSR_WRITE, CSR_OP, CSR_DATAFROM};
endmodule

module CSR_DMX (
  input  [6:0] in_1,
  output CSR_DATAFROM,
  output [1:0] CSR_OP,
  output CSR_WRITE,
  output TRAP_ECALL,
  output TRAP_EBREAK,
  output TRAP_MRET
);


  assign CSR_DATAFROM = in_1[0];
  assign CSR_OP = in_1[2:1];
  assign CSR_WRITE = in_1[3];
  assign TRAP_EBREAK = in_1[5];
  assign TRAP_ECALL = in_1[4];
  assign TRAP_MRET = in_1[6];
endmodule

module test (
  input  [1:0] in_1,
  input  in_2,
  input  [5:0] in_3,
  input  in_4,
  input  [2:0] in_5,
  input  in_6,
  input  in_7,
  input  [1:0] in_8,
  input  in_9,
  input  in_10,
  input  in_11,
  input  in_12,
  input  in_13,
  input  in_14,
  input  [1:0] in_15,
  input  in_16,
  input  [1:0] in_17,
  input  in_18,
  input  in_19,
  input  in_20,
  input  [6:0] in_21,
  input  in_22,
  input  in_23,
  input  [1:0] in_24,
  input  in_25,
  input  in_26,
  input  in_27,
  input  in_28
);

  wire basic_controlbits_dmx_1_alu_calc, basic_controlbits_dmx_1_alu_y_datafrom,
       basic_controlbits_dmx_1_mem_addrfrom, basic_controlbits_dmx_1_mem_datafrom,
       basic_controlbits_dmx_1_mem_read, basic_controlbits_dmx_1_mem_signext,
       basic_controlbits_dmx_1_mem_write, basic_controlbits_dmx_1_pc_write, basic_controlbits_dmx_1_reg_read,
       basic_controlbits_dmx_1_reg_write, csr_dmx_1_trap_mret, undriven;
  wire [1:0] basic_controlbits_dmx_1_alu_x_datafrom, basic_controlbits_dmx_1_mem_mode,
       basic_controlbits_dmx_1_reg_datafrom, csr_dmx_1_csr_op;
  wire [2:0] basic_controlbits_dmx_1_pc_datafrom;
  wire [5:0] basic_controlbits_dmx_1_alu_op;
  wire [6:0] csr_mux_1_out_7;
  wire [12:0] floating_controlbits_mux_1_floating_controlbits;
  wire [24:0] basic_controlbits_mux_1_basic_controlbits;

  Basic_ControlBits_MUX basic_controlbits_mux_1 (
    .ALU_X_DATAFROM(in_1), .ALU_Y_DATAFROM(in_2), .ALU_OP(in_3), .ALU_CALC(in_4), .PC_DATAFROM(in_5),
    .PC_WRITE(in_6), .REG_DATAFROM(in_8), .REG_READ(in_9), .REG_WRITE(in_10), .MEM_ADDRFROM(in_11),
    .MEM_DATAFROM(in_12), .MEM_READ(in_13), .MEM_WRITE(in_14),
    .Basic_ControlBits(basic_controlbits_mux_1_basic_controlbits), .MEM_MODE(in_15), .MEM_SIGNEXT(in_16));
  Floating_ControlBits_MUX floating_controlbits_mux_1 (
    .FLREG_DATAFROM(in_17), .FLREG_READ(in_18), .FLREG_WRITE(in_19), .FPU_X_DATAFROM(in_20), .FPU_OP(in_21),
    .FPU_CALC(in_22), .Floating_ControlBits(floating_controlbits_mux_1_floating_controlbits));
  CSR_MUX csr_mux_1 (
    .CSR_DATAFROM(in_23), .CSR_OP(in_24), .CSR_WRITE(in_25), .TRAP_ECALL(in_26), .TRAP_EBREAK(in_27),
    .out_7(csr_mux_1_out_7), .TRAP_MRET(in_28));
  Floating_ControlBits_DMX floating_controlbits_dmx_1 (.Floating_ControlBits(floating_controlbits_mux_1_floating_controlbits));  // open: FLREG_DATAFROM, FLREG_READ, FLREG_WRITE, FPU_X_DATAFROM, FPU_OP, FPU_CALC
  CSR_DMX csr_dmx_1 (
    .in_1(csr_mux_1_out_7), .CSR_OP(csr_dmx_1_csr_op), .TRAP_MRET(csr_dmx_1_trap_mret));  // open: CSR_DATAFROM, CSR_WRITE, TRAP_ECALL, TRAP_EBREAK
  Basic_ControlBits_DMX basic_controlbits_dmx_1 (
    .Basic_ControlBits(basic_controlbits_mux_1_basic_controlbits),
    .ALU_X_DATAFROM(basic_controlbits_dmx_1_alu_x_datafrom),
    .ALU_Y_DATAFROM(basic_controlbits_dmx_1_alu_y_datafrom), .ALU_OP(basic_controlbits_dmx_1_alu_op),
    .ALU_CALC(basic_controlbits_dmx_1_alu_calc), .PC_DATAFROM(basic_controlbits_dmx_1_pc_datafrom),
    .PC_WRITE(basic_controlbits_dmx_1_pc_write), .REG_DATAFROM(basic_controlbits_dmx_1_reg_datafrom),
    .REG_READ(basic_controlbits_dmx_1_reg_read), .REG_WRITE(basic_controlbits_dmx_1_reg_write),
    .MEM_ADDRFROM(basic_controlbits_dmx_1_mem_addrfrom), .MEM_DATAFROM(basic_controlbits_dmx_1_mem_datafrom),
    .MEM_READ(basic_controlbits_dmx_1_mem_read), .MEM_WRITE(basic_controlbits_dmx_1_mem_write),
    .MEM_MODE(basic_controlbits_dmx_1_mem_mode), .MEM_SIGNEXT(basic_controlbits_dmx_1_mem_signext));
  // Probe on csr_dmx_1_csr_op
  // Probe on basic_controlbits_dmx_1_alu_x_datafrom
  // Probe on basic_controlbits_dmx_1_alu_y_datafrom
  // Probe on basic_controlbits_dmx_1_alu_op
  // Probe on basic_controlbits_dmx_1_alu_calc
  // Probe on basic_controlbits_dmx_1_pc_datafrom
  // Probe on basic_controlbits_dmx_1_pc_write
  // Probe on undriven
  // Probe on basic_controlbits_dmx_1_reg_datafrom
  // Probe on basic_controlbits_dmx_1_reg_read
  // Probe on basic_controlbits_dmx_1_reg_write
  // Probe on basic_controlbits_dmx_1_mem_addrfrom
  // Probe on basic_controlbits_dmx_1_mem_datafrom
  // Probe on basic_controlbits_dmx_1_mem_read
  // Probe on basic_controlbits_dmx_1_mem_write
  // Probe on basic_controlbits_dmx_1_mem_mode
  // Probe on basic_controlbits_dmx_1_mem_signext
endmodule
