// Logisim project INTERRUPT.circ as structural Verilog: 2 circuits, main circuit Interrupt Controller
module Interrupt_Controller (
  input  ECALL_0,
  input  EXTRA_1,
  input  KEYBD_2,
  input  FAULT_3,
  input  EBRK_4,
  input  [31:0] MIP_IN,
  input  [31:0] MIE_IN,
  input  [31:0] MSTATUS_IN,
  input  [31:0] MTVEC_IN,
  input  [31:0] PC_IN,
  input  MRET,
  input  CLK,
  output [31:0] MIP_OUT,
  output [1:0] MIP_OP,
  output RESPOND,
  output [31:0] PC_OUT,
  output [31:0] MEPC_OUT,
  output [1:0] MEPC_OP,
  output [31:0] MSTATUS_OUT,
  output [1:0] MSTATUS_OP
);

  wire comparator_1_eq;
  wire [1:0] ISSUE_MIP_OP, multiplexer_4_out;
  wire [4:0] int_gen_1_intout, INTNO;
  wire [31:0] and_1_out, and_2_out, bit_extender_1_out, bit_extender_3_out, ISSUE_MIP_OUT, RESPOND_MIP_OUT,
       shifter_2_out;

  Int_Gen int_gen_1 (.CLK(CLK), .IntIn(ECALL_0), .RST(MIP_IN[0]), .IntOut(int_gen_1_intout[0]));  // open: Hold
  Int_Gen int_gen_2 (.CLK(CLK), .IntIn(EXTRA_1), .RST(MIP_IN[1]), .IntOut(int_gen_1_intout[1]));  // open: Hold
  Int_Gen int_gen_3 (.CLK(CLK), .IntIn(KEYBD_2), .RST(MIP_IN[2]), .IntOut(int_gen_1_intout[2]));  // open: Hold
  Int_Gen int_gen_4 (.CLK(CLK), .IntIn(FAULT_3), .RST(MIP_IN[3]), .IntOut(int_gen_1_intout[3]));  // open: Hold
  Int_Gen int_gen_5 (.CLK(CLK), .IntIn(EBRK_4), .RST(MIP_IN[4]), .IntOut(int_gen_1_intout[4]));  // open: Hold
  Register #(.width(32), .trigger("rising"), .Select("low")) register_1 (
    .D(PC_IN), .Q(MEPC_OUT), .clk(CLK));  // open: en, clr
  assign and_1_out = MIP_IN & MIE_IN;  // AND_Gate and_1, 32 bits wide
  assign bit_extender_1_out = {{31{MSTATUS_IN[0]}}, MSTATUS_IN[0]};  // Bit_Extender bit_extender_1
  assign ISSUE_MIP_OUT = {{27{1'b0}}, int_gen_1_intout};  // Bit_Extender bit_extender_2
  Comparator #(.width(32), .mode("twosComplement")) comparator_1 (
    .a(ISSUE_MIP_OUT), .b({32{1'b0}}), .eq(comparator_1_eq));  // open: gt, lt
  Shifter #(.width(32), .shift("ll")) shifter_1 (.in(32'h1), .\dist (INTNO), .out(RESPOND_MIP_OUT));
  assign and_2_out = and_1_out & bit_extender_1_out;  // AND_Gate and_2, 32 bits wide
  assign bit_extender_3_out = {{27{1'b0}}, INTNO};  // Bit_Extender bit_extender_3
  Multiplexer #(.select(1), .width(2), .disabled("Z"), .enable("false")) multiplexer_1 (
    .in0(2'b10), .in1(2'b00), .out(ISSUE_MIP_OP), .sel(comparator_1_eq));
  Shifter #(.width(32), .shift("ll")) shifter_2 (.in(bit_extender_3_out), .\dist (5'b00010), .out(shifter_2_out));
  BitFinder #(.width(32), .\type ("high1")) bitfinder_1 (.in(and_2_out), .index(INTNO), .found(RESPOND));
  Adder #(.width(32)) adder_1 (.a(shifter_2_out), .b(MTVEC_IN), .out(PC_OUT), .cin(1'b0));  // open: cout
  Multiplexer #(.select(1), .width(32), .disabled("Z"), .enable("false")) multiplexer_2 (
    .in0(ISSUE_MIP_OUT), .in1(RESPOND_MIP_OUT), .out(MIP_OUT), .sel(RESPOND));
  Multiplexer #(.select(1), .width(2), .disabled("Z"), .enable("false")) multiplexer_3 (
    .in0(ISSUE_MIP_OP), .in1(2'b11), .out(MIP_OP), .sel(RESPOND));
  Multiplexer #(.select(1), .width(2), .disabled("Z"), .enable("false")) multiplexer_4 (
    .in0(2'b00), .in1(2'b10), .out(multiplexer_4_out), .sel(MRET));
  Multiplexer #(.select(1), .width(2), .disabled("Z"), .enable("false")) multiplexer_5 (
    .in0(2'b00), .in1(2'b01), .out(MEPC_OP), .sel(RESPOND));
  Multiplexer #(.select(1), .width(2), .disabled("Z"), .enable("false")) multiplexer_6 (
    .in0(multiplexer_4_out), .in1(2'b11), .out(MSTATUS_OP), .sel(RESPOND));

  assign MSTATUS_OUT = 32'h1;

  // Other names for the same wires on the sheet: ENTRY[31:0] = PC_OUT
endmodule

module Int_Gen (
  input  CLK,
  input  IntIn,
  input  RST,
  output IntOut,
  output Hold
);

  wire and_1_out, and_2_out, d_ff_1_q, or_2_out;

  D_Flip_Flop #(.trigger("rising"), .Pre_Clr_Positions("LEGACY"), .NegatePresetClear("false"), .enable("true"), .NewFFLayout("false")) d_ff_1 (
    .clk(and_1_out), .D(1'b1), .Q(d_ff_1_q), .reset(IntOut));  // open: Qn, preset, en
  and and_1 (and_1_out, ~CLK, IntIn);  // AND_Gate
  or or_1 (Hold, IntOut, d_ff_1_q);
  or or_2 (or_2_out, d_ff_1_q, IntOut);
  D_Flip_Flop #(.trigger("rising"), .Pre_Clr_Positions("LEGACY"), .NegatePresetClear("false"), .enable("true"), .NewFFLayout("false")) d_ff_2 (
    .clk(CLK), .D(and_2_out), .Q(IntOut));  // open: Qn, preset, en, reset
  and and_2 (and_2_out, or_2_out, ~RST);  // AND_Gate
endmodule
