// Logisim project main.circ as structural Verilog: 3 circuits, main circuit Computer
module Computer (
);

  wire CLK, DISP_Clr, DISP_Wr, keyboard_1_avail, MTX_Write, riscv_soc_1_invsig, riscv_soc_1_kbd_clear,
       riscv_soc_1_kbd_readen, riscv_soc_1_tty_clear, riscv_soc_1_tty_write;
  wire [4:0] MTX_Address;
  wire [6:0] keyboard_1_data, riscv_soc_1_tty_wrdata;
  wire [29:0] DISP_Data;
  wire [31:0] matrix_driver_1_row0, matrix_driver_1_row1, matrix_driver_1_row2, matrix_driver_1_row3,
       matrix_driver_1_row4, matrix_driver_1_row5, matrix_driver_1_row6, matrix_driver_1_row7,
       matrix_driver_1_row8, matrix_driver_1_row9, matrix_driver_1_row10, matrix_driver_1_row11,
       matrix_driver_1_row12, matrix_driver_1_row13, matrix_driver_1_row14, matrix_driver_1_row15,
       matrix_driver_1_row16, matrix_driver_1_row17, matrix_driver_1_row18, matrix_driver_1_row19,
       matrix_driver_1_row20, matrix_driver_1_row21, matrix_driver_1_row22, matrix_driver_1_row23,
       matrix_driver_1_row24, matrix_driver_1_row25, matrix_driver_1_row26, matrix_driver_1_row27,
       matrix_driver_1_row28, matrix_driver_1_row29, matrix_driver_1_row30, matrix_driver_1_row31, MTX_WrData;

  Clock #(.highDuration(1), .lowDuration(1)) clock_1 (.out(CLK));
  Keyboard #(.Char_bit_width(7), .buflen(32), .trigger("rising")) keyboard_1 (
    .clk(CLK), .re(riscv_soc_1_kbd_readen), .clr(riscv_soc_1_kbd_clear), .avail(keyboard_1_avail),
    .data(keyboard_1_data));
  DotMatrix #(.inputtype("row"), .matrixcols(32), .matrixrows(32), .persist(0), .dotshape("square")) dotmatrix_1 (
    .row0(matrix_driver_1_row0), .row1(matrix_driver_1_row1), .row2(matrix_driver_1_row2),
    .row3(matrix_driver_1_row3), .row4(matrix_driver_1_row4), .row5(matrix_driver_1_row5),
    .row6(matrix_driver_1_row6), .row7(matrix_driver_1_row7), .row8(matrix_driver_1_row8),
    .row9(matrix_driver_1_row9), .row10(matrix_driver_1_row10), .row11(matrix_driver_1_row11),
    .row12(matrix_driver_1_row12), .row13(matrix_driver_1_row13), .row14(matrix_driver_1_row14),
    .row15(matrix_driver_1_row15), .row16(matrix_driver_1_row16), .row17(matrix_driver_1_row17),
    .row18(matrix_driver_1_row18), .row19(matrix_driver_1_row19), .row20(matrix_driver_1_row20),
    .row21(matrix_driver_1_row21), .row22(matrix_driver_1_row22), .row23(matrix_driver_1_row23),
    .row24(matrix_driver_1_row24), .row25(matrix_driver_1_row25), .row26(matrix_driver_1_row26),
    .row27(matrix_driver_1_row27), .row28(matrix_driver_1_row28), .row29(matrix_driver_1_row29),
    .row30(matrix_driver_1_row30), .row31(matrix_driver_1_row31));
  MATRIX_Driver matrix_driver_1 (
    .Address(MTX_Address), .WrData(MTX_WrData), .WrEn(MTX_Write), .CLK(CLK), .ROW0(matrix_driver_1_row0),
    .ROW1(matrix_driver_1_row1), .ROW2(matrix_driver_1_row2), .ROW3(matrix_driver_1_row3),
    .ROW4(matrix_driver_1_row4), .ROW5(matrix_driver_1_row5), .ROW6(matrix_driver_1_row6),
    .ROW7(matrix_driver_1_row7), .ROW8(matrix_driver_1_row8), .ROW9(matrix_driver_1_row9),
    .ROW10(matrix_driver_1_row10), .ROW11(matrix_driver_1_row11), .ROW12(matrix_driver_1_row12),
    .ROW13(matrix_driver_1_row13), .ROW14(matrix_driver_1_row14), .ROW15(matrix_driver_1_row15),
    .ROW16(matrix_driver_1_row16), .ROW17(matrix_driver_1_row17), .ROW18(matrix_driver_1_row18),
    .ROW19(matrix_driver_1_row19), .ROW20(matrix_driver_1_row20), .ROW21(matrix_driver_1_row21),
    .ROW22(matrix_driver_1_row22), .ROW23(matrix_driver_1_row23), .ROW24(matrix_driver_1_row24),
    .ROW25(matrix_driver_1_row25), .ROW26(matrix_driver_1_row26), .ROW27(matrix_driver_1_row27),
    .ROW28(matrix_driver_1_row28), .ROW29(matrix_driver_1_row29), .ROW30(matrix_driver_1_row30),
    .ROW31(matrix_driver_1_row31));
  RISCV_SoC riscv_soc_1 (
    .KBD_RdData(keyboard_1_data), .KBD_AVAIL(keyboard_1_avail), .TTY_WrData(riscv_soc_1_tty_wrdata),
    .TTY_Write(riscv_soc_1_tty_write), .TTY_Clear(riscv_soc_1_tty_clear),
    .KBD_ReadEn(riscv_soc_1_kbd_readen), .KBD_Clear(riscv_soc_1_kbd_clear), .DISP_WrData(DISP_Data),
    .DISP_Write(DISP_Wr), .DISP_Clear(DISP_Clr), .CLK(CLK), .INVSig(riscv_soc_1_invsig),
    .MTX_WrData(MTX_WrData), .MTX_Write(MTX_Write), .MTX_Addr(MTX_Address));
  TTY #(.Char_bit_width(7), .rows(8), .cols(32), .trigger("rising")) tty_1 (
    .data(riscv_soc_1_tty_wrdata), .clk(CLK), .we(riscv_soc_1_tty_write), .clr(riscv_soc_1_tty_clear));
  // LCD_Video lcd_video_1: pin names not known; wires that end beside it: DISP_Clr, CLK, DISP_Wr, DISP_Data[6:0], DISP_Data[13:7], DISP_Data[29:14]
endmodule

module RISCV_SoC (
  input  [6:0] KBD_RdData,
  input  KBD_AVAIL,
  input  CLK,
  output INVSig,
  output [6:0] TTY_WrData,
  output TTY_Write,
  output TTY_Clear,
  output KBD_ReadEn,
  output KBD_Clear,
  output [29:0] DISP_WrData,
  output DISP_Write,
  output DISP_Clear,
  output [31:0] MTX_WrData,
  output MTX_Write,
  output [4:0] MTX_Addr
);

  wire ALU_CALC, ALU_Y_DATAFROM, clock_1_out, comparator_1_eq, comparator_1_lt, CSR_DATAFROM, CSR_INV,
       CSR_WRITE, d_ff_1_q, MEM_ADDRFROM, MEM_DATAFROM, MEM_READ, MEM_SIGNEXT, MEM_WRITE, MMU_INV,
       nand_1_out, PC_WRITE, REG_READ, REG_WRITE, RESPOND, TRAP_EBREAK, TRAP_ECALL, TRAP_MRET;
  wire [1:0] ALU_X_DATAFROM, CSR_OP, FRM_num, MEM_MODE, MEPC_OP, MIP_OP, MSTATUS_OP, REG_DATAFROM;
  wire [2:0] PC_DATAFROM;
  wire [4:0] FRS3_num, RD_num, RS1_num, RS2_num;
  wire [5:0] ALU_OP, ALU_STATUS;
  wire [6:0] CSRCTRL;
  wire [12:0] CNT_num, FloatCTRL;
  wire [24:0] BasicCTRL;
  wire [31:0] ALU_RESULT, BccPath, bit_extender_1_out, CSR_OUT, CSRs_MCYCLE, CSRs_MEPC, CSRs_MIE,
       CSRs_MINSTR, CSRs_MIP, CSRs_MSTATUS, CSRs_MTVAL, CSRs_MTVEC, EXCEPTION_PC_OUT, Immed, JALRPath,
       MEM_OUT, MEPC_OUT, MIP_OUT, MSTATUS_OUT, multiplexer_2_out, multiplexer_3_out, multiplexer_4_out,
       multiplexer_5_out, multiplexer_6_out, multiplexer_7_out, multiplexer_8_out, Original_NextPC, PC, PC_4,
       rom_1_data, RS1Value, RS2Value, shifter_1_out;

  Multiplexer #(.select(3), .width(32), .disabled("Z"), .enable("false")) multiplexer_1 (
    .in0(PC_4), .in1(BccPath), .in2(BccPath), .in3(JALRPath), .in4(CSRs_MEPC), .out(Original_NextPC),
    .sel(PC_DATAFROM));  // open: in5, in6, in7
  D_Flip_Flop #(.trigger("high"), .Pre_Clr_Positions("LEGACY"), .NegatePresetClear("false"), .enable("true"), .NewFFLayout("false")) d_ff_1 (.Q(d_ff_1_q));  // open: clk, D, Qn, preset, en, reset
  // Probe on 13'h608
  Multiplexer #(.select(1), .width(32), .disabled("Z"), .enable("false")) multiplexer_2 (
    .in0(Original_NextPC), .in1(EXCEPTION_PC_OUT), .out(multiplexer_2_out), .sel(RESPOND));
  Comparator #(.width(13), .mode("twosComplement")) comparator_1 (
    .a(CNT_num), .b(13'h608), .eq(comparator_1_eq), .lt(comparator_1_lt));  // open: gt
  Clock #(.highDuration(1), .lowDuration(1)) clock_1 (.out(clock_1_out));
  Register #(.width(32), .trigger("rising"), .Select("low")) u_PC (
    .D(multiplexer_2_out), .en(PC_WRITE), .Q(PC), .clk(CLK));  // open: clr
  nand nand_1 (nand_1_out, d_ff_1_q, comparator_1_eq);
  Counter #(.width(13), .max('h1fff), .ongoal("stay"), .trigger("rising"), .behavior("old")) counter_1 (
    .count(comparator_1_lt), .Q(CNT_num), .clk(clock_1_out));  // open: load, D, carry, clr, preset
  Shifter #(.width(32), .shift("ll")) shifter_1 (.in(Immed), .\dist (5'b00001), .out(shifter_1_out));
  Adder #(.width(32)) adder_1 (.a(Immed), .b(RS1Value), .out(JALRPath), .cin(1'b0));  // open: cout
  Controlled_Buffer #(.width(1), .negatecontrol("false")) controlled_buffer_1 (
    .in(clock_1_out), .en(nand_1_out));  // open: out
  Pull_Resistor #(.pull(1)) pull_resistor_1 (.node(CLK));
  ROM #(.addrWidth(10), .dataWidth(32), .Select("high")) rom_1 (.addr(PC[11:2]), .data(rom_1_data));
  Adder #(.width(32)) adder_2 (.a(PC), .b(32'h4), .out(PC_4), .cin(1'b0));  // open: cout
  Adder #(.width(32)) adder_3 (.a(shifter_1_out), .b(PC), .out(BccPath), .cin(1'b0));  // open: cout
  Multiplexer #(.select(1), .width(32), .disabled("Z"), .enable("false")) multiplexer_3 (
    .in0(ALU_RESULT), .in1(PC), .out(multiplexer_3_out), .sel(MEM_ADDRFROM));
  Multiplexer #(.select(1), .width(32), .disabled("Z"), .enable("false")) multiplexer_4 (
    .in0(RS2Value), .out(multiplexer_4_out), .sel(MEM_DATAFROM));  // open: in1
  Interrupt_Controller interrupt_controller_1 (
    .ECALL_0(TRAP_ECALL), .EXTRA_1(1'b0), .KEYBD_2(KBD_AVAIL), .FAULT_3(INVSig), .EBRK_4(TRAP_EBREAK),
    .MIP_IN(CSRs_MIP), .MIE_IN(CSRs_MIE), .MSTATUS_IN(CSRs_MSTATUS), .MTVEC_IN(CSRs_MTVEC),
    .PC_IN(Original_NextPC), .MRET(TRAP_MRET), .CLK(CLK), .MIP_OUT(MIP_OUT), .MIP_OP(MIP_OP),
    .RESPOND(RESPOND), .PC_OUT(EXCEPTION_PC_OUT), .MEPC_OUT(MEPC_OUT), .MEPC_OP(MEPC_OP),
    .MSTATUS_OUT(MSTATUS_OUT), .MSTATUS_OP(MSTATUS_OP));
  DECODER decoder_1 (
    .INSTR(rom_1_data), .ALU_COMP_STATUS(ALU_STATUS), .BasicControl(BasicCTRL), .FloatControl(FloatCTRL),
    .CSRControl(CSRCTRL), .Immed(Immed), .RS1(RS1_num), .RS2(RS2_num), .RD(RD_num), .FLOAT_FRS3(FRS3_num),
    .FLOAT_RM(FRM_num));
  Multiplexer #(.select(2), .width(32), .disabled("Z"), .enable("false")) multiplexer_5 (
    .in0(RS1Value), .in1(PC_4), .in2({32{1'b0}}), .in3(PC), .out(multiplexer_5_out), .sel(ALU_X_DATAFROM));
  Multiplexer #(.select(1), .width(32), .disabled("Z"), .enable("false")) multiplexer_6 (
    .in0(RS2Value), .in1(Immed), .out(multiplexer_6_out), .sel(ALU_Y_DATAFROM));
  MMU mmu_1 (
    .Address(multiplexer_3_out), .WriteData(multiplexer_4_out), .Read(MEM_READ), .Write(MEM_WRITE),
    .Mode(MEM_MODE), .SignExt(MEM_SIGNEXT), .KBD_RdData(KBD_RdData), .KBD_AVAIL(KBD_AVAIL), .CLK(CLK),
    .TTY_WrData(TTY_WrData), .TTY_Write(TTY_Write), .TTY_Clear(TTY_Clear), .KBD_ReadEn(KBD_ReadEn),
    .KBD_Clear(KBD_Clear), .DISP_WrData(DISP_WrData), .DISP_Write(DISP_Write), .DISP_Clear(DISP_Clear),
    .INV(MMU_INV), .Out(MEM_OUT), .MTX_WrData(MTX_WrData), .MTX_Write(MTX_Write), .MTX_WrAddr(MTX_Addr));
  assign bit_extender_1_out = {{27{1'b0}}, RS1_num};  // Bit_Extender bit_extender_1
  Multiplexer #(.select(1), .width(32), .disabled("Z"), .enable("false")) multiplexer_7 (
    .in0(RS1Value), .in1(bit_extender_1_out), .out(multiplexer_7_out), .sel(CSR_DATAFROM));
  ALU alu_1 (
    .X(multiplexer_5_out), .Y(multiplexer_6_out), .CLK(CLK), .Start(ALU_CALC), .ALUOP(ALU_OP),
    .RES(ALU_RESULT), .Status(ALU_STATUS));  // open: Working, Invalid
  Basic_ControlBits_DMX basic_controlbits_dmx_1 (
    .Basic_ControlBits(BasicCTRL), .ALU_X_DATAFROM(ALU_X_DATAFROM), .ALU_Y_DATAFROM(ALU_Y_DATAFROM),
    .ALU_OP(ALU_OP), .ALU_CALC(ALU_CALC), .PC_DATAFROM(PC_DATAFROM), .PC_WRITE(PC_WRITE),
    .REG_DATAFROM(REG_DATAFROM), .REG_READ(REG_READ), .REG_WRITE(REG_WRITE), .MEM_ADDRFROM(MEM_ADDRFROM),
    .MEM_DATAFROM(MEM_DATAFROM), .MEM_READ(MEM_READ), .MEM_WRITE(MEM_WRITE), .MEM_MODE(MEM_MODE),
    .MEM_SIGNEXT(MEM_SIGNEXT));
  CSR_DMX csr_dmx_1 (
    .in_1(CSRCTRL), .CSR_DATAFROM(CSR_DATAFROM), .CSR_OP(CSR_OP), .CSR_WRITE(CSR_WRITE),
    .TRAP_ECALL(TRAP_ECALL), .TRAP_EBREAK(TRAP_EBREAK), .TRAP_MRET(TRAP_MRET));
  Multiplexer #(.select(2), .width(32), .disabled("Z"), .enable("false")) multiplexer_8 (
    .in0(ALU_RESULT), .in1(MEM_OUT), .in3(CSR_OUT), .out(multiplexer_8_out), .sel(REG_DATAFROM));  // open: in2
  // RegisterFile registerfile_1: pin names not known; wires that end beside it: multiplexer_8_out, CLK, REG_WRITE, RD_num, RS1_num, RS2_num, RS1Value, RS2Value
  CSR_Interface csr_interface_1 (
    .SYNC_DATA(multiplexer_7_out), .SYNC_ADDR(Immed[11:0]), .SYNC_WRITE(CSR_WRITE), .SYNC_OP(CSR_OP),
    .MSTATUS_IN(MSTATUS_OUT), .MSTATUS_OP(MSTATUS_OP), .MEPC_IN(MEPC_OUT), .MEPC_OP(MEPC_OP),
    .MTVAL_IN({32{1'b0}}), .MTVAL_OP(2'b00), .MIP_IN(MIP_OUT), .MIP_OP(MIP_OP), .MCYCLE_CNTUP(1'b0),
    .MINSTRET_CNTUP(1'b0), .CLK(CLK), .MSTATUS(CSRs_MSTATUS), .MIE(CSRs_MIE), .MTVEC(CSRs_MTVEC),
    .MEPC(CSRs_MEPC), .MTVAL(CSRs_MTVAL), .MIP(CSRs_MIP), .MCYCLE(CSRs_MCYCLE), .MINSTRET(CSRs_MINSTR),
    .SYNC_Invalid(CSR_INV), .SYNC_OUT(CSR_OUT));
  and and_1 (INVSig, MMU_INV, CLK);

  // Other names for the same wires on the sheet: JALPath[31:0] = BccPath; MTX_Address[4:0] = MTX_Addr

  // Notes on the sheet:
  //   控制位
  //   暂停节拍，不能为0
  //   用这个时钟源需要去掉电路中的其他时钟源
  //   戳工具置1进入计数暂停模式，ctrl+k时钟自动运行到对应节拍暂停
  //   ctrl+k关闭时钟连续运行，将控制位置零，进入单步调试模式调试
  //   可计数暂停的时钟源
  //   contents of rom_1 (hex, n*v repeats v):
  //   ff4137 ffc10113 97 1808093 30509073 3000e073 14d000ef 6f 140006f 180006f 1c0006f 1200006f 1240006f
  //   128000ef 30200073 12c000ef 30200073 f7c10113 112223 212423 312623 412823 512a23 612c23 712e23
  //   2812023 2912223 2a12423 2b12623 2c12823 2d12a23 2e12c23 2f12e23 5012023 5112223 5212423 5312623
  //   5412823 5512a23 5612c23 5712e23 7812023 7912223 7a12423 7b12623 7c12823 7d12a23 7e12c23 7f12e23
  //   b0000ef 412083 812103 c12183 1012203 1412283 1812303 1c12383 2012403 2412483 2812503 2c12583 3012603
  //   3412683 3812703 3c12783 4012803 4412883 4812903 4c12983 5012a03 5412a83 5812b03 5c12b83 6012c03
  //   6412c83 6812d03 6c12d83 7012e03 7412e83 7812f03 7c12f83 8410113 30200073 74000ef 30200073 78000ef
  //   30200073 1537 b1450513 800006f 1537 b2450513 740006f 1537 ff010113 b3450513 112623 60000ef c0006f
  //   180000ef 48000ef 168000ef fe051ae3 a00513 38000ef 34427073 13 13 34427073 c12083 1010113 8067 1537
  //   b4450513 1c0006f 1537 b5450513 100006f ffff07b7 a7a023 8067 54783 78c63 ffff0737 f72023 154783
  //   150513 fe079ae3 8067 fe010113 812c23 112e23 912a23 50413 4055a63 2d00793 ffff0737 f72023 40a00433
  //   2b444b3 6904063 a00793 8b7d263 17b7 b6478793 2b46433 ffff0737 878433 44783 f72023 1c12083 1812403
  //   1412483 2010113 8067 fc0510e3 3000793 ffff0737 f72023 1c12083 1812403 1412483 2010113 8067 2b4c533
  //   a05863 b12623 f69ff0ef c12583 a00793 2b4e4b3 2b7ca63 3048493 ffff07b7 97a023 ffff07b7 2b46433
  //   3040413 87a023 1c12083 1812403 1412483 2010113 8067 17b7 b6478793 9784b3 4c703 ffff06b7 e6a023
  //   f4dff06f ffff0537 f450513 52503 8067 ffff0537 f050513 52503 8067 ffff0537 f450713 72783 fe078ee3
  //   f050513 52503 8067 ffff06b7 f468713 f068593 a00613 72783 fe078ee3 5a783 c78a63 f50023 f6a023 150513
  //   fe5ff06f 50023 c6a023 8067 54783 50693 2078063 793 178793 f68733 74703 78513 fe0718e3 8067 513 8067
  //   5c783 50713 78c63 f70023 15c783 170713 158593 fe0798e3 70023 8067 2060a63 c50633 50793 5c703 178793
  //   158593 fee78fa3 c78e63 fe0716e3 78023 178793 fec79ce3 8067 8067 8067 54783 50713 513 2078463 59663
  //   180006f a58c63 150513 a707b3 7c783 fe0798e3 8067 8067 8067 54783 2078c63 50793 17c703 178793
  //   fe071ce3 5c703 70c63 e78023 15c703 178793 158593 fe0718e3 78023 8067 50793 fd9ff06f 54783 5c703
  //   e79e63 150513 158593 78863 fe0714e3 f73533 8067 fff00513 fee7fae3 8067 e060063 40a007b3 fff60713
  //   500693 ff5f593 37f793 ee6fa63 c078a63 b50023 100713 ae78e63 b500a3 300713 ce79663 b50123 300313
  //   300893 859813 40f60e33 105e833 1059693 d866b3 1859713 f507b3 ffce7813 e6e733 f806b3 e7a023 478793
  //   fed79ce3 ffce7713 e30333 11707b3 6ee0c63 650333 b30023 178713 4c77663 e50733 b70023 278713 2c77e63
  //   e50733 b70023 378713 2c77663 e50733 b70023 478713 c77e63 e50733 b70023 578793 c7f663 f507b3 b78023
  //   8067 100313 100893 f59ff06f 313 893 f4dff06f 8067 200893 200313 f3dff06f 793 313 f75ff06f fff60893
  //   a060a63 158693 40d50733 373713 98b793 174713 17c793 f777b3 6078863 b567b3 37f793 6079263 ffc67813
  //   58793 50713 b80833 7a683 478793 470713 fed72e23 ff0798e3 ffc67793 f50733 f585b3 40f888b3 4f60863
  //   5c783 f70023 4088263 15c683 100793 d700a3 2f88a63 25c783 f70123 8067 c50633 50793 80006f 168693
  //   5c703 178793 68593 fee78fa3 fec796e3 8067 2060463 c58633 54703 5c783 150513 158593 f70663 e7ee63
  //   f76863 feb612e3 513 8067 fff00513 8067 100513 8067 17b7 b7878793 7a583 47a603 87a683 c7a703 107c783
  //   fd010113 c10513 2112623 b12623 c12823 d12a23 e12c23 f10e23 ae1ff0ef 2c12083 3010113 8067 17b7
  //   b9c78793 7a583 47a603 87a683 c7d703 e7c783 fe010113 10513 112e23 b12023 c12223 d12423 e11623 f10723
  //   a95ff0ef 1537 b8c50513 a89ff0ef 1000593 29a00513 a9dff0ef 1c12083 2010113 8067 ff010113 812423
  //   112623 413 a00593 40513 a75ff0ef 7800513 a41ff0ef a00593 40513 a61ff0ef 3d00513 a2dff0ef 2840533
  //   a00593 140413 a49ff0ef a00513 a15ff0ef a00793 faf41ee3 c12083 812403 1010113 8067 15b7 fd010113
  //   b8858593 2812423 2112623 50413 c8dff0ef 51a63 2c12083 2812403 3010113 8067 15b7 bac58593 40513
  //   c69ff0ef 51e63 1537 bf850513 2812403 2c12083 3010113 9adff06f 15b7 bb458593 40513 c3dff0ef 4051063
  //   17b7 b7878793 7a583 47a603 87a683 c7a703 107c783 c10513 b12623 c12823 d12a23 e12c23 f10e23 961ff0ef
  //   f79ff06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
endmodule

module MATRIX_Driver (
  input  [4:0] Address,
  input  [31:0] WrData,
  input  WrEn,
  input  CLK,
  output [31:0] ROW0,
  output [31:0] ROW1,
  output [31:0] ROW2,
  output [31:0] ROW3,
  output [31:0] ROW4,
  output [31:0] ROW5,
  output [31:0] ROW6,
  output [31:0] ROW7,
  output [31:0] ROW8,
  output [31:0] ROW9,
  output [31:0] ROW10,
  output [31:0] ROW11,
  output [31:0] ROW12,
  output [31:0] ROW13,
  output [31:0] ROW14,
  output [31:0] ROW15,
  output [31:0] ROW16,
  output [31:0] ROW17,
  output [31:0] ROW18,
  output [31:0] ROW19,
  output [31:0] ROW20,
  output [31:0] ROW21,
  output [31:0] ROW22,
  output [31:0] ROW23,
  output [31:0] ROW24,
  output [31:0] ROW25,
  output [31:0] ROW26,
  output [31:0] ROW27,
  output [31:0] ROW28,
  output [31:0] ROW29,
  output [31:0] ROW30,
  output [31:0] ROW31
);

  wire demultiplexer_1_out0, demultiplexer_1_out1, demultiplexer_1_out2, demultiplexer_1_out3,
       demultiplexer_1_out4, demultiplexer_1_out5, demultiplexer_1_out6, demultiplexer_1_out7,
       demultiplexer_1_out8, demultiplexer_1_out9, demultiplexer_1_out10, demultiplexer_1_out11,
       demultiplexer_1_out12, demultiplexer_1_out13, demultiplexer_1_out14, demultiplexer_1_out15,
       demultiplexer_1_out16, demultiplexer_1_out17, demultiplexer_1_out18, demultiplexer_1_out19,
       demultiplexer_1_out20, demultiplexer_1_out21, demultiplexer_1_out22, demultiplexer_1_out23,
       demultiplexer_1_out24, demultiplexer_1_out25, demultiplexer_1_out26, demultiplexer_1_out27,
       demultiplexer_1_out28, demultiplexer_1_out29, demultiplexer_1_out30, demultiplexer_1_out31;

  Demultiplexer #(.select(5), .width(1), .tristate("false"), .disabled("Z"), .enable("false")) demultiplexer_1 (
    .out0(demultiplexer_1_out0), .out1(demultiplexer_1_out1), .out2(demultiplexer_1_out2),
    .out3(demultiplexer_1_out3), .out4(demultiplexer_1_out4), .out5(demultiplexer_1_out5),
    .out6(demultiplexer_1_out6), .out7(demultiplexer_1_out7), .out8(demultiplexer_1_out8),
    .out9(demultiplexer_1_out9), .out10(demultiplexer_1_out10), .out11(demultiplexer_1_out11),
    .out12(demultiplexer_1_out12), .out13(demultiplexer_1_out13), .out14(demultiplexer_1_out14),
    .out15(demultiplexer_1_out15), .out16(demultiplexer_1_out16), .out17(demultiplexer_1_out17),
    .out18(demultiplexer_1_out18), .out19(demultiplexer_1_out19), .out20(demultiplexer_1_out20),
    .out21(demultiplexer_1_out21), .out22(demultiplexer_1_out22), .out23(demultiplexer_1_out23),
    .out24(demultiplexer_1_out24), .out25(demultiplexer_1_out25), .out26(demultiplexer_1_out26),
    .out27(demultiplexer_1_out27), .out28(demultiplexer_1_out28), .out29(demultiplexer_1_out29),
    .out30(demultiplexer_1_out30), .out31(demultiplexer_1_out31), .in(WrEn), .sel(Address));
  Register #(.width(32), .trigger("rising"), .Select("low")) register_1 (
    .D(WrData), .en(demultiplexer_1_out0), .Q(ROW0), .clk(CLK));  // open: clr
  Register #(.width(32), .trigger("rising"), .Select("low")) register_2 (
    .D(WrData), .en(demultiplexer_1_out2), .Q(ROW2), .clk(CLK));  // open: clr
  Register #(.width(32), .trigger("rising"), .Select("low")) register_3 (
    .D(WrData), .en(demultiplexer_1_out4), .Q(ROW4), .clk(CLK));  // open: clr
  Register #(.width(32), .trigger("rising"), .Select("low")) register_4 (
    .D(WrData), .en(demultiplexer_1_out6), .Q(ROW6), .clk(CLK));  // open: clr
  Register #(.width(32), .trigger("rising"), .Select("low")) register_5 (
    .D(WrData), .en(demultiplexer_1_out8), .Q(ROW8), .clk(CLK));  // open: clr
  Register #(.width(32), .trigger("rising"), .Select("low")) register_6 (
    .D(WrData), .en(demultiplexer_1_out10), .Q(ROW10), .clk(CLK));  // open: clr
  Register #(.width(32), .trigger("rising"), .Select("low")) register_7 (
    .D(WrData), .en(demultiplexer_1_out12), .Q(ROW12), .clk(CLK));  // open: clr
  Register #(.width(32), .trigger("rising"), .Select("low")) register_8 (
    .D(WrData), .en(demultiplexer_1_out14), .Q(ROW14), .clk(CLK));  // open: clr
  Register #(.width(32), .trigger("rising"), .Select("low")) register_9 (
    .D(WrData), .en(demultiplexer_1_out16), .Q(ROW16), .clk(CLK));  // open: clr
  Register #(.width(32), .trigger("rising"), .Select("low")) register_10 (
    .D(WrData), .en(demultiplexer_1_out18), .Q(ROW18), .clk(CLK));  // open: clr
  Register #(.width(32), .trigger("rising"), .Select("low")) register_11 (
    .D(WrData), .en(demultiplexer_1_out20), .Q(ROW20), .clk(CLK));  // open: clr
  Register #(.width(32), .trigger("rising"), .Select("low")) register_12 (
    .D(WrData), .en(demultiplexer_1_out22), .Q(ROW22), .clk(CLK));  // open: clr
  Register #(.width(32), .trigger("rising"), .Select("low")) register_13 (
    .D(WrData), .en(demultiplexer_1_out24), .Q(ROW24), .clk(CLK));  // open: clr
  Register #(.width(32), .trigger("rising"), .Select("low")) register_14 (
    .D(WrData), .en(demultiplexer_1_out26), .Q(ROW26), .clk(CLK));  // open: clr
  Register #(.width(32), .trigger("rising"), .Select("low")) register_15 (
    .D(WrData), .en(demultiplexer_1_out28), .Q(ROW28), .clk(CLK));  // open: clr
  Register #(.width(32), .trigger("rising"), .Select("low")) register_16 (
    .D(WrData), .en(demultiplexer_1_out30), .Q(ROW30), .clk(CLK));  // open: clr
  Register #(.width(32), .trigger("rising"), .Select("low")) register_17 (
    .D(WrData), .en(demultiplexer_1_out1), .Q(ROW1), .clk(CLK));  // open: clr
  Register #(.width(32), .trigger("rising"), .Select("low")) register_18 (
    .D(WrData), .en(demultiplexer_1_out3), .Q(ROW3), .clk(CLK));  // open: clr
  Register #(.width(32), .trigger("rising"), .Select("low")) register_19 (
    .D(WrData), .en(demultiplexer_1_out5), .Q(ROW5), .clk(CLK));  // open: clr
  Register #(.width(32), .trigger("rising"), .Select("low")) register_20 (
    .D(WrData), .en(demultiplexer_1_out7), .Q(ROW7), .clk(CLK));  // open: clr
  Register #(.width(32), .trigger("rising"), .Select("low")) register_21 (
    .D(WrData), .en(demultiplexer_1_out9), .Q(ROW9), .clk(CLK));  // open: clr
  Register #(.width(32), .trigger("rising"), .Select("low")) register_22 (
    .D(WrData), .en(demultiplexer_1_out11), .Q(ROW11), .clk(CLK));  // open: clr
  Register #(.width(32), .trigger("rising"), .Select("low")) register_23 (
    .D(WrData), .en(demultiplexer_1_out13), .Q(ROW13), .clk(CLK));  // open: clr
  Register #(.width(32), .trigger("rising"), .Select("low")) register_24 (
    .D(WrData), .en(demultiplexer_1_out15), .Q(ROW15), .clk(CLK));  // open: clr
  Register #(.width(32), .trigger("rising"), .Select("low")) register_25 (
    .D(WrData), .en(demultiplexer_1_out17), .Q(ROW17), .clk(CLK));  // open: clr
  Register #(.width(32), .trigger("rising"), .Select("low")) register_26 (
    .D(WrData), .en(demultiplexer_1_out19), .Q(ROW19), .clk(CLK));  // open: clr
  Register #(.width(32), .trigger("rising"), .Select("low")) register_27 (
    .D(WrData), .en(demultiplexer_1_out21), .Q(ROW21), .clk(CLK));  // open: clr
  Register #(.width(32), .trigger("rising"), .Select("low")) register_28 (
    .D(WrData), .en(demultiplexer_1_out23), .Q(ROW23), .clk(CLK));  // open: clr
  Register #(.width(32), .trigger("rising"), .Select("low")) register_29 (
    .D(WrData), .en(demultiplexer_1_out25), .Q(ROW25), .clk(CLK));  // open: clr
  Register #(.width(32), .trigger("rising"), .Select("low")) register_30 (
    .D(WrData), .en(demultiplexer_1_out27), .Q(ROW27), .clk(CLK));  // open: clr
  Register #(.width(32), .trigger("rising"), .Select("low")) register_31 (
    .D(WrData), .en(demultiplexer_1_out29), .Q(ROW29), .clk(CLK));  // open: clr
  Register #(.width(32), .trigger("rising"), .Select("low")) register_32 (
    .D(WrData), .en(demultiplexer_1_out31), .Q(ROW31), .clk(CLK));  // open: clr

  // Other names for the same wires on the sheet: AddrSel[4:0] = Address

  // Notes on the sheet:
  //   Register Array
endmodule
